// Digital circuit 74LS151.dig as structural Verilog
module _74LS151 (
  input  A,
  input  B,
  input  C,
  input  S,
  input  D0,
  input  D1,
  input  D2,
  input  D3,
  input  D4,
  input  D5,
  input  D6,
  input  D7,
  output Y,
  output W
);

  wire multiplexer_1_out;

  Multiplexer #(.Selector_Bits(3)) multiplexer_1 (
    .sel({C, B, A}), .in_0(D0), .in_1(D1), .in_2(D2), .in_3(D3), .in_4(D4), .in_5(D5), .in_6(D6), .in_7(D7),
    .out(multiplexer_1_out));
  and and_1 (Y, ~S, multiplexer_1_out);  // And
  not not_1 (W, Y);

  // Notes on the sheet:
  //   Y: pin 5
  //   W: pin 6
  //   A: pin 11
  //   B: pin 10
  //   C: pin 9
  //   S: pin 7
  //   D0: pin 4
  //   D1: pin 3
  //   D2: pin 2
  //   D3: pin 1
  //   D4: pin 15
  //   D5: pin 14
  //   D6: pin 13
  //   D7: pin 12
endmodule
