// Digital circuit 74LS273.dig as structural Verilog
module _74LS273 (
  input  CP,
  input  nMR,
  input  D0,
  input  D1,
  input  D2,
  input  D3,
  input  D4,
  input  D5,
  input  D6,
  input  D7,
  output Q0,
  output Q1,
  output Q2,
  output Q3,
  output Q4,
  output Q5,
  output Q6,
  output Q7
);

  wire not_1_out;

  not not_1 (not_1_out, nMR);
  D_FF_AS d_ff_as_1 (.Set(1'b0), .D(D0), .C(CP), .Clr(not_1_out), .Q(Q0));  // open: nQ
  D_FF_AS d_ff_as_2 (.Set(1'b0), .D(D1), .C(CP), .Clr(not_1_out), .Q(Q1));  // open: nQ
  D_FF_AS d_ff_as_3 (.Set(1'b0), .D(D2), .C(CP), .Clr(not_1_out), .Q(Q2));  // open: nQ
  D_FF_AS d_ff_as_4 (.Set(1'b0), .D(D3), .C(CP), .Clr(not_1_out), .Q(Q3));  // open: nQ
  D_FF_AS d_ff_as_5 (.Set(1'b0), .D(D4), .C(CP), .Clr(not_1_out), .Q(Q4));  // open: nQ
  D_FF_AS d_ff_as_6 (.Set(1'b0), .D(D5), .C(CP), .Clr(not_1_out), .Q(Q5));  // open: nQ
  D_FF_AS d_ff_as_7 (.Set(1'b0), .D(D6), .C(CP), .Clr(not_1_out), .Q(Q6));  // open: nQ
  D_FF_AS d_ff_as_8 (.Set(1'b0), .D(D7), .C(CP), .Clr(not_1_out), .Q(Q7));  // open: nQ

  // Notes on the sheet:
  //   CP: pin 11
  //   nMR: pin 1, default 1
  //   D0: pin 3
  //   D1: pin 4
  //   D2: pin 7
  //   D3: pin 8
  //   D4: pin 13
  //   D5: pin 14
  //   D6: pin 17
  //   D7: pin 18
  //   Q0: pin 2
  //   Q1: pin 5
  //   Q2: pin 6
  //   Q3: pin 9
  //   Q4: pin 12
  //   Q5: pin 15
  //   Q6: pin 16
  //   Q7: pin 19
endmodule
