// Digital circuit 74LS540.dig as structural Verilog
module _74LS540 (
  input  nOE1,
  input  nOE2,
  input  _0D,
  input  _1D,
  input  _2D,
  input  _3D,
  input  _4D,
  input  _5D,
  input  _6D,
  input  _7D,
  output n0O,
  output n1O,
  output n2O,
  output n3O,
  output n4O,
  output n5O,
  output n6O,
  output n7O
);

  wire nor_1_out, not_1_out, not_2_out, not_3_out, not_4_out, not_5_out, not_6_out, not_7_out, not_8_out;

  nor nor_1 (nor_1_out, nOE1, nOE2);
  not not_1 (not_1_out, _0D);
  not not_2 (not_2_out, _1D);
  not not_3 (not_3_out, _2D);
  not not_4 (not_4_out, _3D);
  not not_5 (not_5_out, _4D);
  not not_6 (not_6_out, _5D);
  not not_7 (not_7_out, _6D);
  not not_8 (not_8_out, _7D);
  assign n0O = nor_1_out ? not_1_out : 1'bz;  // Driver driver_1
  assign n1O = nor_1_out ? not_2_out : 1'bz;  // Driver driver_2
  assign n2O = nor_1_out ? not_3_out : 1'bz;  // Driver driver_3
  assign n3O = nor_1_out ? not_4_out : 1'bz;  // Driver driver_4
  assign n4O = nor_1_out ? not_5_out : 1'bz;  // Driver driver_5
  assign n5O = nor_1_out ? not_6_out : 1'bz;  // Driver driver_6
  assign n6O = nor_1_out ? not_7_out : 1'bz;  // Driver driver_7
  assign n7O = nor_1_out ? not_8_out : 1'bz;  // Driver driver_8

  // Notes on the sheet:
  //   nOE1: pin 1
  //   nOE2: pin 19
  //   _0D: pin 2
  //   n0O: pin 18
  //   _1D: pin 3
  //   n1O: pin 17
  //   _2D: pin 4
  //   n2O: pin 16
  //   _3D: pin 5
  //   n3O: pin 15
  //   _4D: pin 6
  //   n4O: pin 14
  //   _5D: pin 7
  //   n5O: pin 13
  //   _6D: pin 8
  //   n6O: pin 12
  //   _7D: pin 9
  //   n7O: pin 11
endmodule
