// Digital circuit 74LS563.dig as structural Verilog
module _74LS563 (
  input  D0,
  input  D1,
  input  D2,
  input  D3,
  input  D4,
  input  D5,
  input  D6,
  input  D7,
  input  LE,
  input  nOE,
  output nQ0,
  output nQ1,
  output nQ2,
  output nQ3,
  output nQ4,
  output nQ5,
  output nQ6,
  output nQ7
);

  wire _74373_d_inc_1_pin11, _74373_d_inc_1_pin13, _74373_d_inc_1_pin15, _74373_d_inc_1_pin17,
       _74373_d_inc_2_pin11, _74373_d_inc_3_pin11, _74373_d_inc_4_pin11, _74373_d_inc_5_pin9,
       _74373_d_inc_5_pin10, _74373_d_inc_5_pin11, _74373_d_inc_5_pin12, _74373_d_inc_7_p1,
       _74373_d_inc_7_p2, _74373_d_inc_7_p3, _74373_d_inc_7_p4, _74373_d_inc_7_p5, _74373_d_inc_8_p1,
       undriven, undriven_2;

  _74373_D_inc _74373_d_inc_1 (
    .pin1(D0), .pin2(LE), .pin3(D1), .pin4(LE), .pin5(D2), .pin6(LE), .pin7(D3), .pin8(LE), .pin9(D4),
    .pin10(LE), .pin11(_74373_d_inc_1_pin11), .pin12(nOE), .pin13(_74373_d_inc_1_pin13), .pin14(nOE),
    .pin15(_74373_d_inc_1_pin15), .pin16(nOE), .pin17(_74373_d_inc_1_pin17), .pin18(nOE), .pin20(nOE));  // open: pin19
  _74373_D_inc _74373_d_inc_2 (
    .pin1(D1), .pin2(LE), .pin3(D2), .pin4(LE), .pin5(D3), .pin6(LE), .pin7(D4), .pin8(LE), .pin9(D5),
    .pin10(LE), .pin11(_74373_d_inc_2_pin11), .pin12(nOE), .pin13(_74373_d_inc_1_pin11), .pin14(nOE),
    .pin15(_74373_d_inc_1_pin13), .pin16(nOE), .pin17(_74373_d_inc_1_pin15), .pin18(nOE),
    .pin19(_74373_d_inc_1_pin17), .pin20(nOE));
  _74373_D_inc _74373_d_inc_3 (
    .pin1(D2), .pin2(LE), .pin3(D3), .pin4(LE), .pin5(D4), .pin6(LE), .pin7(D5), .pin8(LE), .pin9(D6),
    .pin10(LE), .pin11(_74373_d_inc_3_pin11), .pin12(nOE), .pin13(_74373_d_inc_2_pin11), .pin14(nOE),
    .pin15(_74373_d_inc_1_pin11), .pin16(nOE), .pin17(_74373_d_inc_1_pin13), .pin18(nOE),
    .pin19(_74373_d_inc_1_pin15), .pin20(nOE));
  _74373_D_inc _74373_d_inc_4 (
    .pin1(D3), .pin2(LE), .pin3(D4), .pin4(LE), .pin5(D5), .pin6(LE), .pin7(D6), .pin8(LE), .pin9(D7),
    .pin10(LE), .pin11(_74373_d_inc_4_pin11), .pin12(nOE), .pin13(_74373_d_inc_3_pin11), .pin14(nOE),
    .pin15(_74373_d_inc_2_pin11), .pin16(nOE), .pin17(_74373_d_inc_1_pin11), .pin18(nOE),
    .pin19(_74373_d_inc_1_pin13), .pin20(nOE));
  _74373_D_inc _74373_d_inc_5 (
    .pin1(D4), .pin2(LE), .pin3(D5), .pin4(LE), .pin5(D6), .pin6(LE), .pin7(D7), .pin8(LE),
    .pin9(_74373_d_inc_5_pin9), .pin10(_74373_d_inc_5_pin10), .pin11(_74373_d_inc_5_pin11),
    .pin12(_74373_d_inc_5_pin12), .pin13(_74373_d_inc_4_pin11), .pin14(nOE), .pin15(_74373_d_inc_3_pin11),
    .pin16(nOE), .pin17(_74373_d_inc_2_pin11), .pin18(nOE), .pin19(_74373_d_inc_1_pin11), .pin20(nOE));
  _74373_D_inc _74373_d_inc_6 (
    .pin1(D5), .pin2(LE), .pin3(D6), .pin4(LE), .pin5(D7), .pin6(LE), .pin7(_74373_d_inc_5_pin9),
    .pin8(_74373_d_inc_5_pin10), .pin13(_74373_d_inc_5_pin11), .pin14(_74373_d_inc_5_pin12),
    .pin15(_74373_d_inc_4_pin11), .pin16(nOE), .pin17(_74373_d_inc_3_pin11), .pin18(nOE),
    .pin19(_74373_d_inc_2_pin11), .pin20(nOE));  // open: pin9, pin10, pin11, pin12
  // _74373_D_inc _74373_d_inc_7: pin names not known; wires that end beside it: _74373_d_inc_7_p1, _74373_d_inc_7_p2, _74373_d_inc_7_p3, _74373_d_inc_7_p4, _74373_d_inc_7_p5
  // _74373_D_inc _74373_d_inc_8: pin names not known; wires that end beside it: _74373_d_inc_8_p1
  assign nQ0 = ~nOE ? undriven : 1'bz;  // DriverInvSel driverinvsel_1
  assign nQ1 = ~nOE ? undriven_2 : 1'bz;  // DriverInvSel driverinvsel_2
  assign nQ2 = ~nOE ? _74373_d_inc_7_p1 : 1'bz;  // DriverInvSel driverinvsel_3
  assign nQ3 = ~nOE ? _74373_d_inc_7_p2 : 1'bz;  // DriverInvSel driverinvsel_4
  assign nQ4 = ~nOE ? _74373_d_inc_7_p3 : 1'bz;  // DriverInvSel driverinvsel_5
  assign nQ5 = ~nOE ? _74373_d_inc_7_p4 : 1'bz;  // DriverInvSel driverinvsel_6
  assign nQ6 = ~nOE ? _74373_d_inc_7_p5 : 1'bz;  // DriverInvSel driverinvsel_7
  assign nQ7 = ~nOE ? _74373_d_inc_8_p1 : 1'bz;  // DriverInvSel driverinvsel_8

  // Notes on the sheet:
  //   D0: pin 2
  //   D1: pin 3
  //   nQ0: pin 19
  //   nQ1: pin 18
  //   nQ2: pin 17
  //   nQ3: pin 16
  //   nQ4: pin 15
  //   nQ5: pin 14
  //   nQ6: pin 13
  //   nQ7: pin 12
  //   D2: pin 4
  //   D3: pin 5
  //   D4: pin 6
  //   D5: pin 7
  //   D6: pin 8
  //   D7: pin 9
  //   LE: pin 11, default 1
  //   nOE: pin 1
endmodule
