// Digital circuit 74LS564.dig as structural Verilog
module _74LS564 (
  input  nOC,
  input  CLK,
  input  D0,
  input  D1,
  input  D2,
  input  D3,
  input  D4,
  input  D5,
  input  D6,
  input  D7,
  output nQ0,
  output nQ1,
  output nQ2,
  output nQ3,
  output nQ4,
  output nQ5,
  output nQ6,
  output nQ7,
  output [7:0] nSPY,
  output [7:0] SPY
);

  D_FF #(.Bits(8)) d_ff_1 (.D({D7, D6, D5, D4, D3, D2, D1, D0}), .C(CLK), .Q(SPY), .nQ(nSPY));
  assign {nQ7, nQ6, nQ5, nQ4, nQ3, nQ2, nQ1, nQ0} = ~nOC ? nSPY : 8'bz;  // DriverInvSel driverinvsel_1
  // Pins of 1 and 8 bits meet at SPY
  // Pins of 1 and 8 bits meet at nSPY

  // Notes on the sheet:
  //   nQ0: pin 19
  //   nQ1: pin 18
  //   nQ2: pin 17
  //   nQ3: pin 16
  //   nOC: pin 1, default 1
  //   CLK: pin 11
  //   nQ4: pin 15
  //   nQ5: pin 14
  //   nQ6: pin 13
  //   nQ7: pin 12
  //   D0: pin 2
  //   D1: pin 3
  //   D2: pin 4
  //   D3: pin 5
  //   D4: pin 6
  //   D5: pin 7
  //   D6: pin 8
  //   D7: pin 9
endmodule
