// Digital circuit 74LS574.dig as structural Verilog
module _74LS574 (
  input  nOC,
  input  CLK,
  input  D0,
  input  D1,
  input  D2,
  input  D3,
  input  D4,
  input  D5,
  input  D6,
  input  D7,
  output Q0,
  output Q1,
  output Q2,
  output Q3,
  output Q4,
  output Q5,
  output Q6,
  output Q7
);

  wire [7:0] d_ff_1_q;

  D_FF #(.Bits(8)) d_ff_1 (.D({D7, D6, D5, D4, D3, D2, D1, D0}), .C(CLK), .Q(d_ff_1_q));  // open: nQ
  assign {Q7, Q6, Q5, Q4, Q3, Q2, Q1, Q0} = ~nOC ? d_ff_1_q : 8'bz;  // DriverInvSel driverinvsel_1

  // Notes on the sheet:
  //   Q0: pin 19
  //   Q1: pin 18
  //   Q2: pin 17
  //   Q3: pin 16
  //   nOC: pin 1, default 1
  //   CLK: pin 11
  //   Q4: pin 15
  //   Q5: pin 14
  //   Q6: pin 13
  //   Q7: pin 12
  //   D0: pin 2
  //   D1: pin 3
  //   D2: pin 4
  //   D3: pin 5
  //   D4: pin 6
  //   D5: pin 7
  //   D6: pin 8
  //   D7: pin 9
endmodule
