// Digital circuit 74LS595.dig as structural Verilog
module _74LS595 (
  input  SER,
  input  SCLK,
  input  RCLK,
  input  nOE,
  input  nCLR,
  output Q_A,
  output Q_B,
  output Q_C,
  output Q_D,
  output Q_E,
  output Q_F,
  output Q_G,
  output Q_H,
  output Q_H_2
);

  wire not_1_out;
  wire [6:0] d_ff_as_1_q;
  wire [7:0] d_ff_1_q;

  not not_1 (not_1_out, nCLR);
  D_FF_AS d_ff_as_1 (.Set(1'b0), .D(SER), .C(SCLK), .Clr(not_1_out), .Q(d_ff_as_1_q[0]));  // open: nQ
  D_FF_AS d_ff_as_2 (.Set(1'b0), .D(d_ff_as_1_q[0]), .C(SCLK), .Clr(not_1_out), .Q(d_ff_as_1_q[1]));  // open: nQ
  D_FF_AS d_ff_as_3 (.Set(1'b0), .D(d_ff_as_1_q[1]), .C(SCLK), .Clr(not_1_out), .Q(d_ff_as_1_q[2]));  // open: nQ
  D_FF_AS d_ff_as_4 (.Set(1'b0), .D(d_ff_as_1_q[2]), .C(SCLK), .Clr(not_1_out), .Q(d_ff_as_1_q[3]));  // open: nQ
  D_FF_AS d_ff_as_5 (.Set(1'b0), .D(d_ff_as_1_q[3]), .C(SCLK), .Clr(not_1_out), .Q(d_ff_as_1_q[4]));  // open: nQ
  D_FF_AS d_ff_as_6 (.Set(1'b0), .D(d_ff_as_1_q[4]), .C(SCLK), .Clr(not_1_out), .Q(d_ff_as_1_q[5]));  // open: nQ
  D_FF_AS d_ff_as_7 (.Set(1'b0), .D(d_ff_as_1_q[5]), .C(SCLK), .Clr(not_1_out), .Q(d_ff_as_1_q[6]));  // open: nQ
  D_FF #(.Bits(8)) d_ff_1 (.D({Q_H_2, d_ff_as_1_q}), .C(RCLK), .Q(d_ff_1_q));  // open: nQ
  D_FF_AS d_ff_as_8 (.Set(1'b0), .D(d_ff_as_1_q[6]), .C(SCLK), .Clr(not_1_out), .Q(Q_H_2));  // open: nQ
  assign {Q_H, Q_G, Q_F, Q_E, Q_D, Q_C, Q_B, Q_A} = ~nOE ? d_ff_1_q : 8'bz;  // DriverInvSel driverinvsel_1

  // Notes on the sheet:
  //   Q_A: pin 15
  //   Q_B: pin 1
  //   Q_C: pin 2
  //   Q_D: pin 3
  //   Q_E: pin 4
  //   Q_F: pin 5
  //   Q_G: pin 6
  //   Q_H: pin 7
  //   Q_H_2: pin 9
  //   SER: pin 14
  //   SCLK: pin 11
  //   RCLK: pin 12
  //   nOE: pin 13
  //   nCLR: pin 10
endmodule
