// Digital circuit Control.dig as structural Verilog
module Control (
  input  XTAL,
  input  TraceClock,
  input  uSTEP,
  input  RUNHALT,
  input  iSTEP,
  input  TRACE,
  input  RESET_F,
  input  RESET_R,
  input  TXBUSY,
  input  HALT,
  input  MOPend,
  output A,
  output B,
  output C,
  output TICK,
  output PC_Flash,
  output nResetP,
  output nReset,
  output CK
);

  wire and_1_out, and_2_out, and_3_out, and_4_out, and_5_out, and_6_out, half7474_1_q, half7474_2_q,
       half7474_3_q, half7474_4_nq, half7474_5_nq, half7474_6_nq, half7474_7_q, half7474_8_nq, half7474_9_nq,
       half7474_10_nq, half7474_10_q, half7474_11_q, half7474_12_q, half7474_13_q, nCK, not_3_out, nPOR,
       or_1_out, or_2_out, or_3_out, or_4_out, POR;

  and and_1 (and_1_out, TRACE, TraceClock);
  or or_1 (or_1_out, RESET_F, POR, RESET_R);
  or or_2 (or_2_out, RUNHALT, iSTEP, and_1_out);
  not not_1 (nCK, XTAL);
  not not_2 (nReset, or_1_out);
  Half7474 half7474_1 (.nSD(1'b1), .D(HALT), .CP(XTAL), .nRD(nResetP), .Q(half7474_1_q));  // open: nQ
  Half7474 half7474_2 (.nSD(1'b1), .D(RUNHALT), .CP(XTAL), .nRD(nResetP), .Q(half7474_2_q));  // open: nQ
  Half7474 half7474_3 (.nSD(1'b1), .D(or_2_out), .CP(XTAL), .nRD(nResetP), .Q(half7474_3_q));  // open: nQ
  RS_FF_AS rs_ff_as_1 (.S(TraceClock), .R(1'b0), .Q(nPOR), .nQ(POR));
  Half7474 half7474_4 (.nSD(1'b1), .D(half7474_1_q), .CP(XTAL), .nRD(nResetP), .nQ(half7474_4_nq));  // open: Q
  Half7474 half7474_5 (.nSD(1'b1), .D(half7474_2_q), .CP(XTAL), .nRD(nResetP), .nQ(half7474_5_nq));  // open: Q
  Half7474 half7474_6 (.nSD(1'b1), .D(half7474_3_q), .CP(XTAL), .nRD(nResetP), .nQ(half7474_6_nq));  // open: Q
  Half7474 half7474_7 (.nSD(1'b1), .D(or_1_out), .CP(XTAL), .nRD(1'b1), .Q(half7474_7_q));  // open: nQ
  and and_2 (and_2_out, half7474_1_q, half7474_4_nq);
  and and_3 (and_3_out, half7474_2_q, half7474_5_nq);
  and and_4 (and_4_out, half7474_3_q, half7474_6_nq);
  not not_3 (not_3_out, and_4_out);
  Half7474 half7474_8 (.nSD(1'b1), .D(half7474_7_q), .CP(XTAL), .nRD(1'b1), .nQ(half7474_8_nq));  // open: Q
  or or_3 (or_3_out, and_2_out, and_3_out);
  Half7474 half7474_9 (.nSD(nResetP), .D(MOPend), .CP(XTAL), .nRD(1'b1), .nQ(half7474_9_nq));  // open: Q
  and and_5 (and_5_out, half7474_7_q, half7474_8_nq);
  Half7474 half7474_10 (
    .nSD(1'b1), .D(half7474_10_nq), .CP(or_3_out), .nRD(nResetP), .Q(half7474_10_q), .nQ(half7474_10_nq));
  Half7474 half7474_11 (.nSD(not_3_out), .D(1'b0), .CP(1'b0), .nRD(half7474_9_nq), .Q(half7474_11_q));  // open: nQ
  not not_4 (nResetP, and_5_out);
  or or_4 (or_4_out, half7474_10_q, half7474_11_q);
  Half7474 half7474_12 (.nSD(1'b1), .D(uSTEP), .CP(nCK), .nRD(nResetP), .Q(half7474_12_q));  // open: nQ
  Half7474 half7474_13 (.nSD(1'b1), .D(or_4_out), .CP(nCK), .nRD(nResetP), .Q(half7474_13_q));  // open: nQ
  LED RUN (.in(half7474_13_q));
  and and_6 (and_6_out, half7474_13_q, XTAL);
  or or_5 (TICK, and_5_out, half7474_12_q, and_6_out);
  _74LS163 _74ls163_1 (
    .nPE(nReset), .nSR(1'b1), .CP(TICK), .CET(1'b1), .CEP(1'b1), .P0(1'b0), .P1(1'b0), .P2(1'b0), .P3(1'b0),
    .Q0(A), .Q1(B), .Q2(C));  // open: TC, Q3

  assign CK = XTAL;
  assign PC_Flash = RESET_F;

  // Other names for the same wires on the sheet: Busy = TXBUSY

  // Notes on the sheet:
  //   XTAL: Hz: 50
  //   TraceClock: Hz: 8
  //   CONTROL/SEQUENCER
endmodule
