// Digital circuit GPIO.dig as structural Verilog
module GPIO (
  input  [23:0] DATAi,
  input  [23:0] ADDR,
  input  AddrCk,
  input  GPIOr,
  input  GPIOw,
  input  UARTdrives,
  output [23:0] DATAo,
  output UARTtrig,
  output UARTread,
  output UARTbusyRead
);

  wire _74ls138_1_ny0, _74ls138_1_ny1, _74ls138_1_ny2, _74ls138_1_ny3, _74ls138_1_ny4, _74ls138_1_ny5,
       _74ls138_1_ny6, _74ls138_1_ny7, _74ls138_2_ny0, _74ls138_2_ny1, _74ls138_2_ny2, _74ls138_2_ny3,
       _74ls138_2_ny4, _74ls138_2_ny5, _74ls138_2_ny6, _74ls138_2_ny7, _74ls175_1_p4, _74ls175_1_p5,
       _74ls175_1_p6, _74ls540_1_n0o, _74ls540_1_n1o, _74ls540_1_n2o, _74ls540_1_n3o, _74ls540_1_n4o,
       _74ls540_1_n5o, _74ls540_1_n6o, _74ls540_1_n7o, not_1_out;
  wire [7:0] _74ls574_1_q7;

  // _74LS175 _74ls175_1: pin names not known; wires that end beside it: 1'b0, AddrCk, 1'b1, _74ls175_1_p4, _74ls175_1_p5, _74ls175_1_p6
  _74LS540 _74ls540_1 (
    .nOE1(1'b0), .nOE2(1'b0), ._0D(ADDR[0]), ._1D(ADDR[1]), ._2D(ADDR[2]), ._3D(ADDR[3]), ._4D(ADDR[4]),
    ._5D(ADDR[5]), ._6D(ADDR[6]), ._7D(ADDR[7]), .n0O(_74ls540_1_n0o), .n1O(_74ls540_1_n1o),
    .n2O(_74ls540_1_n2o), .n3O(_74ls540_1_n3o), .n4O(_74ls540_1_n4o), .n5O(_74ls540_1_n5o),
    .n6O(_74ls540_1_n6o), .n7O(_74ls540_1_n7o));
  not not_1 (not_1_out, GPIOr);
  _74LS138 _74ls138_1 (
    .A(ADDR[0]), .B(ADDR[1]), .C(ADDR[2]), .G(GPIOw), .nGB(1'b0), .nGA(1'b0), .nY0(_74ls138_1_ny0),
    .nY1(_74ls138_1_ny1), .nY2(_74ls138_1_ny2), .nY3(_74ls138_1_ny3), .nY4(_74ls138_1_ny4),
    .nY5(_74ls138_1_ny5), .nY6(_74ls138_1_ny6), .nY7(_74ls138_1_ny7));
  _74LS574 _74ls574_1 (
    .nOC(1'b0), .CLK(_74ls138_1_ny6), .D0(_74ls540_1_n0o), .D1(_74ls540_1_n1o), .D2(_74ls540_1_n2o),
    .D3(_74ls540_1_n3o), .D4(_74ls540_1_n4o), .D5(_74ls540_1_n5o), .D6(_74ls540_1_n6o), .D7(_74ls540_1_n7o),
    .Q0(_74ls574_1_q7[0]), .Q1(_74ls574_1_q7[1]), .Q2(_74ls574_1_q7[2]), .Q3(_74ls574_1_q7[3]),
    .Q4(_74ls574_1_q7[4]), .Q5(_74ls574_1_q7[5]), .Q6(_74ls574_1_q7[6]), .Q7(_74ls574_1_q7[7]));  // open: SPY
  _74LS138 _74ls138_2 (
    .A(_74ls175_1_p4), .B(_74ls175_1_p5), .C(_74ls175_1_p6), .G(GPIOr), .nGB(1'b0), .nGA(1'b0),
    .nY0(_74ls138_2_ny0), .nY1(_74ls138_2_ny1), .nY2(_74ls138_2_ny2), .nY3(_74ls138_2_ny3),
    .nY4(_74ls138_2_ny4), .nY5(_74ls138_2_ny5), .nY6(_74ls138_2_ny6), .nY7(_74ls138_2_ny7));
  // _74LS540 _74ls540_2: pin names not known; wires that end beside it: _74ls138_2_ny6, _74ls138_2_ny6
  _74LS541 _74ls541_1 (
    .nOE1(not_1_out), .nOE2(not_1_out), ._0D(1'b0), ._1D(1'b0), ._2D(1'b0), ._3D(1'b0), ._4D(1'b0),
    ._5D(1'b0), ._6D(1'b0), ._7D(1'b0), ._0O(DATAo[8]), ._1O(DATAo[9]), ._2O(DATAo[10]), ._3O(DATAo[11]),
    ._4O(DATAo[12]), ._5O(DATAo[13]), ._6O(DATAo[14]), ._7O(DATAo[15]));
  _74LS541 _74ls541_2 (
    .nOE1(not_1_out), .nOE2(not_1_out), ._0D(1'b0), ._1D(1'b0), ._2D(1'b0), ._3D(1'b0), ._4D(1'b0),
    ._5D(1'b0), ._6D(1'b0), ._7D(UARTdrives), ._0O(DATAo[16]), ._1O(DATAo[17]), ._2O(DATAo[18]),
    ._3O(DATAo[19]), ._4O(DATAo[20]), ._5O(DATAo[21]), ._6O(DATAo[22]), ._7O(DATAo[23]));
  // Probe on _74ls138_1_ny0
  // Probe on _74ls138_1_ny1
  // Probe on _74ls138_1_ny2
  // Probe on _74ls138_1_ny3
  // Probe on _74ls138_1_ny4
  // Probe on _74ls138_1_ny5
  // Probe on _74ls138_1_ny6
  // Probe on _74ls138_1_ny7
  not not_2 (UARTtrig, _74ls138_1_ny7);
  // Probe on _74ls574_1_q7
  // Probe on _74ls138_2_ny0
  // Probe on _74ls138_2_ny1
  // Probe on _74ls138_2_ny2
  // Probe on _74ls138_2_ny3
  // Probe on _74ls138_2_ny4
  // Probe on _74ls138_2_ny5
  // Probe on _74ls138_2_ny6
  // Probe on _74ls138_2_ny7
  not not_3 (UARTread, _74ls138_2_ny7);
  // Probe on _74ls138_2_ny6
  not not_4 (UARTbusyRead, _74ls138_2_ny0);
endmodule
