// Digital circuit Half7474.dig as structural Verilog
module Half7474 (
  input  nSD,
  input  D,
  input  CP,
  input  nRD,
  output Q,
  output nQ
);

  wire and_1_out, and_2_out, and_3_out, and_4_out, d_ff_as_1_nq, d_ff_as_1_q, delay_1_out, nor_1_out,
       nor_2_out;

  Delay #(.delayTime(2)) delay_1 (.in(CP), .out(delay_1_out));
  and and_1 (and_1_out, ~delay_1_out, CP);  // And
  and and_2 (and_2_out, ~D, and_1_out);  // And
  and and_3 (and_3_out, and_1_out, D);
  and and_4 (and_4_out, ~nRD, ~nSD);  // And
  nor nor_1 (nor_1_out, ~nRD, and_2_out, nor_2_out);  // NOr
  nor nor_2 (nor_2_out, nor_1_out, and_3_out, ~nSD);  // NOr
  D_FF_AS d_ff_as_1 (.Set(~nRD), .D(D), .C(CP), .Clr(~nSD), .Q(d_ff_as_1_q), .nQ(d_ff_as_1_nq));
  or or_1 (Q, and_4_out, nor_1_out);
  or or_2 (nQ, and_4_out, nor_2_out);

  // Notes on the sheet:
  //   Q: pin 5
  //   nQ: pin 6
  //   nSD: pin 4, default 1
  //   D: pin 2, default 1
  //   CP: pin 3
  //   nRD: pin 1, default 1
endmodule
