// Digital circuit Microcode.dig as structural Verilog
module Microcode (
  input  A,
  input  B,
  input  C,
  input  TICK,
  input  AisNeg,
  input  BisNeg,
  input  nReset,
  input  LEQ,
  input  Ena,
  output MopEnd,
  output nEpc,
  output PCck,
  output nPCld,
  output nRD,
  output nWR,
  output AAck,
  output nAAe,
  output AVck,
  output BAck,
  output nBAe,
  output BVck,
  output nRESe,
  output IOw,
  output IOr,
  output nNeg,
  output T4
);

  wire _74ls238_1_y6, _74ls238_1_y7, and_1_out, and_2_out, and_3_out, and_4_out, delay_1_out, nand_1_out,
       nand_2_out, NegRead, NegWrite, nNegRead, nNegWrite, nor_3_out, nor_4_out, nor_7_out, nor_8_out,
       not_1_out, not_2_out, not_3_out, TS0, TS1, TS2, TS3;

  _74LS238 _74ls238_1 (
    .A(A), .B(B), .C(C), .G(Ena), .nGA(1'b0), .nGB(1'b0), .Y0(TS0), .Y1(TS1), .Y2(TS2), .Y3(TS3), .Y4(T4),
    .Y5(MopEnd), .Y6(_74ls238_1_y6), .Y7(_74ls238_1_y7));
  Delay #(.delayTime(2)) delay_1 (.in(not_1_out), .out(delay_1_out));
  not not_1 (not_1_out, not_2_out);
  not not_2 (not_2_out, TICK);
  nand nand_1 (nand_1_out, TS3, not_2_out, BisNeg);
  not not_3 (not_3_out, MopEnd);
  and and_1 (and_1_out, TS3, nNegRead, nNegWrite);
  and and_2 (and_2_out, TS3, 1'b1, NegRead);
  and and_3 (and_3_out, TS3, 1'b1, NegWrite);
  and and_4 (and_4_out, T4, nNegRead, nNegWrite);
  and and_5 (IOr, T4, 1'b1, NegRead);
  and and_6 (IOw, T4, 1'b1, NegWrite);
  Half7474 half7474_1 (.nSD(nand_1_out), .D(1'b0), .CP(nReset), .nRD(not_3_out), .Q(NegWrite), .nQ(nNegWrite));
  nor nor_1 (nEpc, MopEnd, TS2, TS0);
  nor nor_2 (PCck, MopEnd, TS3, TS1);
  nand nand_2 (nand_2_out, TS1, not_2_out, AisNeg);
  nand nand_3 (nPCld, MopEnd, nNeg, LEQ);
  Half7474 half7474_2 (.nSD(nand_2_out), .D(1'b0), .CP(nReset), .nRD(not_3_out), .Q(NegRead), .nQ(nNegRead));
  nor nor_3 (nor_3_out, TS2, TS1, TS0);
  nor nor_4 (nor_4_out, MopEnd, and_1_out, 1'b0);
  and and_7 (nRD, nor_4_out, nor_3_out);
  nor nor_5 (nWR, IOr, and_4_out);
  not not_4 (AAck, TS0);
  not not_5 (nAAe, TS1);
  nor nor_6 (nNeg, NegWrite, NegRead);
  not not_6 (AVck, TS1);
  not not_7 (BAck, TS2);
  nor nor_7 (nor_7_out, and_3_out, and_1_out, IOw);
  nor nor_8 (nor_8_out, IOr, and_4_out, 1'b0);
  and and_8 (nBAe, nor_8_out, nor_7_out);
  not not_8 (BVck, and_1_out);
  nor nor_9 (nRESe, IOw, and_3_out, and_4_out);

  // Other names for the same wires on the sheet: Aaddr_CK = AAck; Aval_CK = AVck; Baddr_CK = BAck; Bval_CK = BVck;
  //   GPIOread = IOr; GPIOwrite = IOw; nAaddr_E = nAAe; nBaddr_E = nBAe; nE_PC = nEpc; nNegg = nNeg; nPC_LD = nPCld;
  //   nResult_E = nRESe; PC_CK = PCck; TS4 = T4; TS5 = MopEnd

  // Notes on the sheet:
  //   MICROCODE
  //   T0
  //   T1
  //   T2
  //   T3
  //   T3NOIO
  //   T3W
  //   T4NOIO
  //   T4R
  //   T4W
  //   T5
endmodule
