// Digital circuit Microcode1.dig as structural Verilog
module Microcode1 (
  input  A,
  input  B,
  input  C,
  input  TICK,
  input  AisNeg,
  input  BisNeg,
  input  nReset,
  input  LEQ,
  input  Ena,
  output MopEnd,
  output nEpc,
  output PCck,
  output nPCld,
  output nRD,
  output nWR,
  output AAck,
  output nAAe,
  output AVck,
  output BAck,
  output nBAe,
  output BVck,
  output nRESe,
  output IOw,
  output IOr,
  output nNeg
);

  wire _74ls238_1_y6, _74ls238_1_y7, and_1_out, and_5_out, and_6_out, and_7_out, and_8_out, and_9_out,
       and_10_out, and_11_out, and_12_out, nand_1_out, nand_2_out, NegRead, NegWrite, nNegRead, nNegWrite,
       not_2_out, not_3_out, Ph1, pullup_1_out, TS0, TS1, TS3, TS4, TS5;

  _74LS238 _74ls238_1 (
    .A(A), .B(B), .C(C), .G(Ena), .nGA(1'b0), .nGB(1'b0), .Y0(TS0), .Y1(TS1), .Y2(BVck), .Y3(TS3), .Y4(TS4),
    .Y5(TS5), .Y6(_74ls238_1_y6), .Y7(_74ls238_1_y7));
  PullUp pullup_1 (.out(pullup_1_out));
  not not_1 (Ph1, TICK);
  not not_2 (not_2_out, pullup_1_out);
  and and_1 (and_1_out, Ph1, TS0);
  and and_2 (AAck, TICK, TS0);
  and and_3 (BAck, Ph1, TS1);
  and and_4 (AVck, TICK, TS1);
  and and_5 (and_5_out, Ph1, BVck);
  and and_6 (and_6_out, TICK, BVck);
  and and_7 (and_7_out, Ph1, TS3);
  and and_8 (and_8_out, TICK, TS3);
  and and_9 (and_9_out, Ph1, TS4);
  and and_10 (and_10_out, TICK, TS4);
  and and_11 (and_11_out, Ph1, TS5);
  and and_12 (and_12_out, TICK, TS5);
  nand nand_1 (nand_1_out, TS3, not_2_out, BisNeg);
  not not_3 (not_3_out, MopEnd);
  nor nor_1 (nRD, 1'b0, 1'b0, 1'b0, TS1, TS0);
  Half7474 half7474_1 (.nSD(nand_1_out), .D(1'b0), .CP(nReset), .nRD(not_3_out), .Q(NegWrite), .nQ(nNegWrite));
  nor nor_2 (nEpc, 1'b0, 1'b0, 1'b0, 1'b0, TS0);
  or or_1 (PCck, BAck, AAck);
  nand nand_2 (nand_2_out, TS1, not_2_out, AisNeg);
  not not_4 (nAAe, BAck);
  Half7474 half7474_2 (.nSD(nand_2_out), .D(1'b0), .CP(nReset), .nRD(not_3_out), .Q(NegRead), .nQ(nNegRead));
  not not_5 (nBAe, AVck);
  nor nor_3 (nNeg, NegWrite, NegRead);
  PullUp pullup_2 (.out(nPCld));
  PullUp pullup_3 (.out(nWR));
  PullUp pullup_4 (.out(nRESe));
  PullDown pulldown_1 (.out(IOw));
  PullDown pulldown_2 (.out(IOr));
  PullUp pullup_5 (.out(nNeg));
  PullDown pulldown_3 (.out(MopEnd));

  // Other names for the same wires on the sheet: Aaddr_CK = AAck; Aval_CK = AVck; Baddr_CK = BAck; GPIOread = IOr;
  //   GPIOwrite = IOw; nAaddr_E = nAAe; nBaddr_E = nBAe; nE_PC = nEpc; nNegg = nNeg; nPC_LD = nPCld;
  //   nResult_E = nRESe; PC_CK = PCck; Ph2 = TICK; Bval_CK = BVck; TS2 = BVck
endmodule
