// Digital circuit OneShot.dig as structural Verilog
module OneShot (
  input  i,
  output o
);

  wire not_1_out, not_2_out, not_3_out;

  not not_1 (not_1_out, not_2_out);
  not not_2 (not_2_out, i);
  not not_3 (not_3_out, not_1_out);
  and and_1 (o, not_3_out, i);
endmodule
