// Digital circuit ProgramCounter.dig as structural Verilog
module ProgramCounter (
  input  [23:0] newPC,
  input  CK,
  input  nLD,
  input  nOE,
  input  BFLASH,
  input  nRESET,
  output [23:0] Q,
  output Neg,
  output [23:0] SPY
);

  wire _74ls157_1_y1, _74ls157_1_y2, _74ls157_1_y3, _74ls157_1_y4, _74ls157_2_y1, _74ls157_2_y2,
       _74ls157_2_y3, _74ls157_2_y4, _74ls157_3_y1, _74ls157_3_y2, _74ls157_3_y3, _74ls157_3_y4,
       _74ls157_4_y1, _74ls157_4_y2, _74ls157_4_y3, _74ls157_4_y4, _74ls157_5_y1, _74ls157_5_y2,
       _74ls157_5_y3, _74ls157_5_y4, _74ls157_6_y1, _74ls157_6_y2, _74ls157_6_y3, _74ls157_6_y4,
       _74ls163_1_tc, _74ls163_2_tc, _74ls163_3_tc, _74ls163_4_tc, _74ls163_5_tc, _74ls163_6_tc, and_1_out,
       and_2_out, and_3_out, and_4_out;

  and and_1 (and_1_out, nRESET, nRESET);
  and and_2 (and_2_out, and_1_out, and_1_out);
  and and_3 (and_3_out, nLD, nRESET);
  and and_4 (and_4_out, CK, nRESET);
  _74LS157 _74ls157_1 (
    .S(and_2_out), .A1(1'b0), .A2(1'b0), .A3(1'b0), .A4(1'b0), .B1(newPC[0]), .B2(newPC[1]), .B3(newPC[2]),
    .B4(newPC[3]), .G(1'b0), .Y1(_74ls157_1_y1), .Y2(_74ls157_1_y2), .Y3(_74ls157_1_y3), .Y4(_74ls157_1_y4));
  _74LS157 _74ls157_2 (
    .S(and_2_out), .A1(1'b0), .A2(1'b0), .A3(1'b0), .A4(1'b0), .B1(newPC[4]), .B2(newPC[5]), .B3(newPC[6]),
    .B4(newPC[7]), .G(1'b0), .Y1(_74ls157_2_y1), .Y2(_74ls157_2_y2), .Y3(_74ls157_2_y3), .Y4(_74ls157_2_y4));
  _74LS157 _74ls157_3 (
    .S(and_2_out), .A1(1'b0), .A2(1'b0), .A3(1'b0), .A4(1'b0), .B1(newPC[8]), .B2(newPC[9]), .B3(newPC[10]),
    .B4(newPC[11]), .G(1'b0), .Y1(_74ls157_3_y1), .Y2(_74ls157_3_y2), .Y3(_74ls157_3_y3), .Y4(_74ls157_3_y4));
  _74LS157 _74ls157_4 (
    .S(and_2_out), .A1(1'b0), .A2(1'b0), .A3(1'b0), .A4(1'b0), .B1(newPC[12]), .B2(newPC[13]),
    .B3(newPC[14]), .B4(newPC[15]), .G(1'b0), .Y1(_74ls157_4_y1), .Y2(_74ls157_4_y2), .Y3(_74ls157_4_y3),
    .Y4(_74ls157_4_y4));
  _74LS157 _74ls157_5 (
    .S(and_2_out), .A1(1'b0), .A2(1'b0), .A3(1'b0), .A4(1'b0), .B1(newPC[16]), .B2(newPC[17]),
    .B3(newPC[18]), .B4(newPC[19]), .G(1'b0), .Y1(_74ls157_5_y1), .Y2(_74ls157_5_y2), .Y3(_74ls157_5_y3),
    .Y4(_74ls157_5_y4));
  _74LS157 _74ls157_6 (
    .S(and_2_out), .A1(1'b0), .A2(BFLASH), .A3(BFLASH), .A4(1'b0), .B1(newPC[20]), .B2(newPC[21]),
    .B3(newPC[22]), .B4(newPC[23]), .G(1'b0), .Y1(_74ls157_6_y1), .Y2(_74ls157_6_y2), .Y3(_74ls157_6_y3),
    .Y4(_74ls157_6_y4));
  _74LS163 _74ls163_1 (
    .nPE(and_3_out), .nSR(1'b1), .CP(and_4_out), .CET(1'b1), .CEP(1'b1), .P0(_74ls157_1_y1),
    .P1(_74ls157_1_y2), .P2(_74ls157_1_y3), .P3(_74ls157_1_y4), .TC(_74ls163_1_tc), .Q0(SPY[0]), .Q1(SPY[1]),
    .Q2(SPY[2]), .Q3(SPY[3]));
  _74LS163 _74ls163_2 (
    .nPE(and_3_out), .nSR(1'b1), .CP(and_4_out), .CET(_74ls163_1_tc), .CEP(1'b1), .P0(_74ls157_2_y1),
    .P1(_74ls157_2_y2), .P2(_74ls157_2_y3), .P3(_74ls157_2_y4), .TC(_74ls163_2_tc), .Q0(SPY[4]), .Q1(SPY[5]),
    .Q2(SPY[6]), .Q3(SPY[7]));
  _74LS163 _74ls163_3 (
    .nPE(and_3_out), .nSR(1'b1), .CP(and_4_out), .CET(_74ls163_2_tc), .CEP(1'b1), .P0(_74ls157_3_y1),
    .P1(_74ls157_3_y2), .P2(_74ls157_3_y3), .P3(_74ls157_3_y4), .TC(_74ls163_3_tc), .Q0(SPY[8]), .Q1(SPY[9]),
    .Q2(SPY[10]), .Q3(SPY[11]));
  _74LS163 _74ls163_4 (
    .nPE(and_3_out), .nSR(1'b1), .CP(and_4_out), .CET(_74ls163_3_tc), .CEP(1'b1), .P0(_74ls157_4_y1),
    .P1(_74ls157_4_y2), .P2(_74ls157_4_y3), .P3(_74ls157_4_y4), .TC(_74ls163_4_tc), .Q0(SPY[12]),
    .Q1(SPY[13]), .Q2(SPY[14]), .Q3(SPY[15]));
  _74LS163 _74ls163_5 (
    .nPE(and_3_out), .nSR(1'b1), .CP(and_4_out), .CET(_74ls163_4_tc), .CEP(1'b1), .P0(_74ls157_5_y1),
    .P1(_74ls157_5_y2), .P2(_74ls157_5_y3), .P3(_74ls157_5_y4), .TC(_74ls163_5_tc), .Q0(SPY[16]),
    .Q1(SPY[17]), .Q2(SPY[18]), .Q3(SPY[19]));
  _74LS163 _74ls163_6 (
    .nPE(and_3_out), .nSR(1'b1), .CP(and_4_out), .CET(_74ls163_5_tc), .CEP(1'b1), .P0(_74ls157_6_y1),
    .P1(_74ls157_6_y2), .P2(_74ls157_6_y3), .P3(_74ls157_6_y4), .TC(_74ls163_6_tc), .Q0(SPY[20]),
    .Q1(SPY[21]), .Q2(SPY[22]), .Q3(Neg));
  // _74LS245 _74ls245_1: pin names not known; wires that end beside it: 1'b1, nOE
  // _74LS245 _74ls245_2: pin names not known; wires that end beside it: 1'b1, nOE
  // _74LS245 _74ls245_3: pin names not known; wires that end beside it: 1'b1, nOE

  assign SPY[23] = Neg;

  // Notes on the sheet:
  //   newPC: default 1193046
  //   nLD: default 1
  //   nOE: default 1
  //   nRESET: default 1
endmodule
