// Digital circuit Register-Normal.dig as structural Verilog
module Register_Normal (
  input  [23:0] D,
  input  AddrCk,
  input  nAddrOE,
  input  ValCk,
  input  nValOE,
  output [23:0] Value,
  output [23:0] Addr,
  output Neg,
  output [23:0] SpyV,
  output [23:0] SpyA
);

  wire and_1_out, and_2_out, and_3_out, and_4_out, and_5_out, reset_1_out;

  and and_1 (and_1_out, D[16], D[17], D[18], D[19]);
  and and_2 (and_2_out, D[20], D[21], D[22], D[23]);
  and and_3 (and_3_out, D[8], D[9], D[10], D[11]);
  and and_4 (and_4_out, D[12], D[13], D[14], D[15]);
  // _74LS574 _74ls574_1: pin names not known; wires that end beside it: nAddrOE, AddrCk
  // _74LS574 _74ls574_2: pin names not known; wires that end beside it: nAddrOE, AddrCk
  // _74LS574 _74ls574_3: pin names not known; wires that end beside it: nAddrOE, AddrCk
  // _74LS574 _74ls574_4: pin names not known; wires that end beside it: nValOE, ValCk
  // _74LS574 _74ls574_5: pin names not known; wires that end beside it: nValOE, ValCk
  // _74LS574 _74ls574_6: pin names not known; wires that end beside it: nValOE, ValCk
  // _74LS574 _74ls574_7: pin names not known; wires that end beside it: 1'b0, AddrCk
  // _74LS574 _74ls574_8: pin names not known; wires that end beside it: 1'b0, AddrCk
  // _74LS574 _74ls574_9: pin names not known; wires that end beside it: 1'b0, AddrCk
  // _74LS574 _74ls574_10: pin names not known; wires that end beside it: 1'b0, ValCk
  // _74LS574 _74ls574_11: pin names not known; wires that end beside it: 1'b0, ValCk
  // _74LS574 _74ls574_12: pin names not known; wires that end beside it: 1'b0, ValCk
  and and_5 (and_5_out, and_1_out, and_2_out, and_3_out, and_4_out);
  Reset reset_1 (.out(reset_1_out));
  // Half7474 half7474_1: pin names not known; wires that end beside it: 1'b1, and_5_out, AddrCk, reset_1_out, Neg

  // Notes on the sheet:
  //   nAddrOE: default 1
  //   nValOE: default 1
endmodule
