// Digital circuit Register.dig as structural Verilog
module Register (
  input  [23:0] D,
  input  CLKaddr,
  input  CLKval,
  input  nOEaddr,
  input  nOEval,
  output [23:0] Addr,
  output [23:0] Value,
  output IO,
  output [23:0] SpyA,
  output [23:0] SpyV
);

  wire and_1_out, and_2_out, and_3_out, and_4_out, and_5_out, and_6_out;

  // _74LS574 _74ls574_1: pin names not known; wires that end beside it: 1'b0, CLKaddr
  // _74LS574 _74ls574_2: pin names not known; wires that end beside it: 1'b0, CLKaddr
  // _74LS574 _74ls574_3: pin names not known; wires that end beside it: 1'b0, CLKaddr
  // _74LS574 _74ls574_4: pin names not known; wires that end beside it: 1'b0, CLKval
  // _74LS574 _74ls574_5: pin names not known; wires that end beside it: 1'b0, CLKval
  // _74LS574 _74ls574_6: pin names not known; wires that end beside it: 1'b0, CLKval
  // _74LS245 _74ls245_1: pin names not known; wires that end beside it: 1'b1, nOEaddr
  // _74LS245 _74ls245_2: pin names not known; wires that end beside it: 1'b1, nOEaddr
  // _74LS245 _74ls245_3: pin names not known; wires that end beside it: 1'b1, nOEaddr
  // _74LS245 _74ls245_4: pin names not known; wires that end beside it: 1'b1, nOEval
  // _74LS245 _74ls245_5: pin names not known; wires that end beside it: 1'b1, nOEval
  // _74LS245 _74ls245_6: pin names not known; wires that end beside it: 1'b1, nOEval
  and and_1 (and_1_out, SpyA[4], SpyA[5], SpyA[6], SpyA[7]);
  and and_2 (and_2_out, SpyA[8], SpyA[9], SpyA[10], SpyA[11]);
  and and_3 (and_3_out, SpyA[12], SpyA[13], SpyA[14], SpyA[15]);
  and and_4 (and_4_out, SpyA[16], SpyA[17], SpyA[18], SpyA[19]);
  and and_5 (and_5_out, SpyA[20], SpyA[21], SpyA[22], SpyA[23]);
  PullDown #(.Bits(24)) pulldown_1 (.out(Value));
  and and_6 (and_6_out, and_1_out, and_2_out, and_3_out, and_4_out);
  and and_7 (IO, and_6_out, and_5_out);

  // Notes on the sheet:
  //   nOEaddr: default 1
  //   nOEval: default 1
endmodule
