// Digital circuit RegisterA.dig as structural Verilog
module RegisterA (
  input  [23:0] D,
  input  CLKaddr,
  input  nOEaddr,
  input  CKval,
  input  nOEval,
  output [23:0] Value,
  output [23:0] Addr,
  output IO
);

  wire and_1_out, and_2_out, and_3_out, and_4_out, and_5_out, reset_1_out;

  and and_1 (and_1_out, D[16], D[17], D[18], D[19]);
  and and_2 (and_2_out, D[20], D[21], D[22], D[23]);
  and and_3 (and_3_out, D[8], D[9], D[10], D[11]);
  and and_4 (and_4_out, D[12], D[13], D[14], D[15]);
  // _74LS574 _74ls574_1: pin names not known; wires that end beside it: nOEaddr, CLKaddr
  // _74LS574 _74ls574_2: pin names not known; wires that end beside it: nOEaddr, CLKaddr
  // _74LS574 _74ls574_3: pin names not known; wires that end beside it: nOEaddr, CLKaddr
  // _74LS564 _74ls564_1: pin names not known; wires that end beside it: nOEval, CKval
  // _74LS564 _74ls564_2: pin names not known; wires that end beside it: nOEval, CKval
  // _74LS564 _74ls564_3: pin names not known; wires that end beside it: nOEval, CKval
  and and_5 (and_5_out, and_1_out, and_2_out, and_3_out, and_4_out);
  Reset reset_1 (.out(reset_1_out));
  // Half7474 half7474_1: pin names not known; wires that end beside it: 1'b1, and_5_out, CLKaddr, reset_1_out, IO
  PullDown #(.Bits(24)) pulldown_1 (.out(Value));

  // Notes on the sheet:
  //   nOEaddr: default 1
  //   nOEval: default 1
endmodule
