// Digital circuit RegisterB.dig as structural Verilog
module RegisterB (
  input  [23:0] D,
  input  CLKaddr,
  input  nOEaddr,
  input  CKval,
  input  nOEval,
  output [23:0] Addr,
  output IO,
  output [23:0] Value
);

  wire and_1_out, and_2_out, and_3_out, and_4_out, and_5_out, and_6_out, and_7_out, and_8_out, and_9_out,
       and_10_out, and_11_out, not_1_out, not_2_out, not_3_out, not_4_out, not_5_out, reset_1_out,
       reset_2_out;

  // _74LS574 _74ls574_1: pin names not known; wires that end beside it: nOEaddr, CLKaddr
  // _74LS574 _74ls574_2: pin names not known; wires that end beside it: nOEaddr, CLKaddr
  // _74LS574 _74ls574_3: pin names not known; wires that end beside it: nOEaddr, CLKaddr
  // _74LS574 _74ls574_4: pin names not known; wires that end beside it: nOEval, CKval
  // _74LS574 _74ls574_5: pin names not known; wires that end beside it: nOEval, CKval
  // _74LS574 _74ls574_6: pin names not known; wires that end beside it: nOEval, CKval
  and and_1 (and_1_out, D[8], D[9], D[10], D[11]);
  and and_2 (and_2_out, D[12], D[13], D[14], D[15]);
  and and_3 (and_3_out, D[16], D[17], D[18], D[19]);
  and and_4 (and_4_out, D[20], D[21], D[22], D[23]);
  and and_5 (and_5_out, and_1_out, and_2_out, and_3_out, and_4_out);
  PullDown #(.Bits(24)) pulldown_1 (.out(Value));
  Reset reset_1 (.out(reset_1_out));
  and and_6 (and_6_out, Addr[8], Addr[9], Addr[10], Addr[11]);
  and and_7 (and_7_out, Addr[12], Addr[13], Addr[14], Addr[15]);
  and and_8 (and_8_out, Addr[16], Addr[17], Addr[18], Addr[19]);
  and and_9 (and_9_out, Addr[20], Addr[21], Addr[22], Addr[23]);
  Half7474 half7474_1 (.nSD(1'b1), .D(and_5_out), .CP(CLKaddr), .nRD(reset_1_out), .Q(IO));  // open: nQ
  not not_1 (not_1_out, nOEaddr);
  not not_2 (not_2_out, not_1_out);
  not not_3 (not_3_out, not_2_out);
  not not_4 (not_4_out, not_3_out);
  and and_10 (and_10_out, and_6_out, and_7_out, and_8_out, and_9_out);
  not not_5 (not_5_out, not_4_out);
  and and_11 (and_11_out, Addr[5], Addr[6], Addr[7], and_10_out);
  Half7474 half7474_2 (.nSD(1'b1), .D(and_11_out), .CP(not_5_out), .nRD(reset_2_out));  // open: Q, nQ
  Reset reset_2 (.out(reset_2_out));

  // Notes on the sheet:
  //   nOEaddr: default 1
  //   nOEval: default 1
endmodule
