// Digital circuit SUBLEQ24-GPIO.dig as structural Verilog
module SUBLEQ24_GPIO (
  input  [23:0] DBUS,
  input  [7:0] GPIO2in,
  input  nIOwriteP,
  input  nIOreadP,
  input  A_ck,
  input  B_ck,
  output [23:0] DBUSo,
  output nUARTrxdRead,
  output nUARTavailRead,
  output nUARTbusyRead,
  output UARTtxdWrite,
  output [7:0] PORT2OUT
);

  wire _74ls138_1_p7, _74ls138_1_p8, _74ls138_1_p9, _74ls138_1_p10, _74ls138_1_p11, _74ls175_1_p3,
       _74ls175_1_p4, _74ls175_1_p5, _74ls175_1_p6, _74ls175_2_p3, _74ls175_2_p4, _74ls175_2_p5,
       _74ls175_2_p6, _74ls238_1_p7, _74ls238_1_p8, _74ls238_1_p9, _74ls238_1_p10, _74ls238_1_p11,
       _74ls238_1_p12, _74ls238_1_p13;

  // Probe on nIOwriteP
  // Probe on nIOreadP
  // _74LS175 _74ls175_1: pin names not known; wires that end beside it: B_ck, 1'b1, _74ls175_1_p3, _74ls175_1_p4, _74ls175_1_p5, _74ls175_1_p6
  // _74LS175 _74ls175_2: pin names not known; wires that end beside it: A_ck, 1'b1, _74ls175_2_p3, _74ls175_2_p4, _74ls175_2_p5, _74ls175_2_p6
  // _74LS238 _74ls238_1: pin names not known; wires that end beside it: _74ls175_1_p3, _74ls175_1_p4, _74ls175_1_p5, 1'b1, _74ls175_1_p6, nIOwriteP, _74ls238_1_p7, _74ls238_1_p8, _74ls238_1_p9, _74ls238_1_p10, _74ls238_1_p11, _74ls238_1_p12, _74ls238_1_p13, UARTtxdWrite
  // _74LS138 _74ls138_1: pin names not known; wires that end beside it: _74ls175_2_p3, _74ls175_2_p4, _74ls175_2_p5, 1'b1, _74ls175_2_p6, nIOreadP, _74ls138_1_p7, _74ls138_1_p8, _74ls138_1_p9, _74ls138_1_p10, _74ls138_1_p11, nUARTbusyRead, nUARTavailRead, nUARTrxdRead
  // _74LS541 _74ls541_1: pin names not known; wires that end beside it: _74ls138_1_p11, _74ls138_1_p11, DBUSo[0], DBUSo[1], DBUSo[2], DBUSo[3], DBUSo[4], DBUSo[5], DBUSo[6], DBUSo[7]
  // _74LS541 _74ls541_2: pin names not known; wires that end beside it: nIOreadP, nIOreadP, 1'b0, 1'b0, 1'b0, 1'b0, 1'b0, 1'b0, 1'b0, 1'b0, DBUSo[8], DBUSo[9], DBUSo[10], DBUSo[11], DBUSo[12], DBUSo[13], DBUSo[14], DBUSo[15]
  // _74LS541 _74ls541_3: pin names not known; wires that end beside it: nIOreadP, nIOreadP, 1'b0, 1'b0, 1'b0, 1'b0, 1'b0, 1'b0, 1'b0, 1'b0, DBUSo[16], DBUSo[17], DBUSo[18], DBUSo[19], DBUSo[20], DBUSo[21], DBUSo[22], DBUSo[23]
  // Probe on _74ls238_1_p7
  // Probe on _74ls238_1_p8
  // Probe on _74ls238_1_p9
  // Probe on _74ls238_1_p10
  // Probe on _74ls238_1_p11
  // Probe on _74ls238_1_p12
  // Probe on _74ls238_1_p13
  // Probe on UARTtxdWrite
  // _74LS564 _74ls564_1: pin names not known; wires that end beside it: 1'b0, _74ls238_1_p11
  // Probe on _74ls138_1_p7
  // Probe on _74ls138_1_p8
  // Probe on _74ls138_1_p9
  // Probe on _74ls138_1_p10
  // Probe on _74ls138_1_p11
  // Probe on nUARTbusyRead
  // Probe on nUARTavailRead
  // Probe on nUARTrxdRead
  // Probe on PORT2OUT

  // Notes on the sheet:
  //   GPIO2in: default 80
  //   GPIO
  //   GPIOw
  //   GPIOr
  //   (-8)
  //   (-7)
  //   (-6)
  //   (-5)
  //   (-4) PORT2Write
  //   (-3)
  //   (-2)
  //   (-1) UARTtxdWrite
  //   (-4) PORT2read
  //   (-3) UARTbusyRead
  //   (-2) UARTavailRead
  //   (-1) UARTrxdRead
endmodule
