// Digital circuit SUBLEQ24-MAR.dig as structural Verilog
module SUBLEQ24_MAR (
  input  [23:0] DBUS,
  input  MAR_CK,
  input  nMAR_E,
  input  nRESET,
  input  TS0,
  input  B_CK,
  input  A_CK,
  output [23:0] ABUS,
  output AisNeg,
  output BisNeg
);

  wire and_1_out, not_1_out;

  not not_1 (not_1_out, TS0);
  and and_1 (and_1_out, not_1_out, nRESET);
  // _74LS574 _74ls574_1: pin names not known; wires that end beside it: nMAR_E, MAR_CK
  // _74LS574 _74ls574_2: pin names not known; wires that end beside it: nMAR_E, MAR_CK
  // _74LS574 _74ls574_3: pin names not known; wires that end beside it: nMAR_E, MAR_CK
  // Half7474 half7474_1: pin names not known; wires that end beside it: 1'b1, DBUS[23], A_CK, and_1_out, AisNeg
  // Half7474 half7474_2: pin names not known; wires that end beside it: 1'b1, DBUS[23], B_CK, and_1_out, BisNeg

  // Notes on the sheet:
  //   MAR & NEG
endmodule
