// Digital circuit SUBLEQ24-PC.dig as structural Verilog
module SUBLEQ24_PC (
  input  [23:0] DBUS,
  input  nResetP,
  input  PC_CK,
  input  nPC_LD,
  input  nE_PC,
  input  PC_FLASH,
  output [23:0] ABUS,
  output PC_neg,
  output [23:0] SPY_PC,
  output PCbit0
);

  wire _74ls157_1_y1, _74ls157_1_y2, _74ls157_1_y3, _74ls157_1_y4, _74ls157_2_y1, _74ls157_2_y2,
       _74ls157_2_y3, _74ls157_2_y4, _74ls157_3_y1, _74ls157_3_y2, _74ls157_3_y3, _74ls157_3_y4,
       _74ls157_4_y1, _74ls157_4_y2, _74ls157_4_y3, _74ls157_4_y4, _74ls157_5_y1, _74ls157_5_y2,
       _74ls157_5_y3, _74ls157_5_y4, _74ls157_6_y1, _74ls157_6_y2, _74ls157_6_y3, _74ls157_6_y4,
       _74ls163_1_tc, _74ls163_2_tc, _74ls163_3_tc, _74ls163_4_tc, _74ls163_5_tc, _74ls163_6_tc, and_1_out,
       delay_1_out, not_1_out, or_1_out;

  Delay #(.delayTime(10)) delay_1 (.in(nResetP), .out(delay_1_out));
  not not_1 (not_1_out, delay_1_out);
  and and_1 (and_1_out, nPC_LD, nResetP);
  or or_1 (or_1_out, PC_CK, not_1_out);
  _74LS157 _74ls157_1 (
    .S(nResetP), .A1(1'b0), .A2(1'b0), .A3(1'b0), .A4(1'b0), .B1(DBUS[0]), .B2(DBUS[1]), .B3(DBUS[2]),
    .B4(DBUS[3]), .G(1'b0), .Y1(_74ls157_1_y1), .Y2(_74ls157_1_y2), .Y3(_74ls157_1_y3), .Y4(_74ls157_1_y4));
  _74LS157 _74ls157_2 (
    .S(nResetP), .A1(1'b0), .A2(1'b0), .A3(1'b0), .A4(1'b0), .B1(DBUS[4]), .B2(DBUS[5]), .B3(DBUS[6]),
    .B4(DBUS[7]), .G(1'b0), .Y1(_74ls157_2_y1), .Y2(_74ls157_2_y2), .Y3(_74ls157_2_y3), .Y4(_74ls157_2_y4));
  _74LS157 _74ls157_3 (
    .S(nResetP), .A1(1'b0), .A2(1'b0), .A3(1'b0), .A4(1'b0), .B1(DBUS[8]), .B2(DBUS[9]), .B3(DBUS[10]),
    .B4(DBUS[11]), .G(1'b0), .Y1(_74ls157_3_y1), .Y2(_74ls157_3_y2), .Y3(_74ls157_3_y3), .Y4(_74ls157_3_y4));
  _74LS157 _74ls157_4 (
    .S(nResetP), .A1(1'b0), .A2(1'b0), .A3(1'b0), .A4(1'b0), .B1(DBUS[12]), .B2(DBUS[13]), .B3(DBUS[14]),
    .B4(DBUS[15]), .G(1'b0), .Y1(_74ls157_4_y1), .Y2(_74ls157_4_y2), .Y3(_74ls157_4_y3), .Y4(_74ls157_4_y4));
  _74LS157 _74ls157_5 (
    .S(nResetP), .A1(1'b0), .A2(1'b0), .A3(1'b0), .A4(1'b0), .B1(DBUS[16]), .B2(DBUS[17]), .B3(DBUS[18]),
    .B4(DBUS[19]), .G(1'b0), .Y1(_74ls157_5_y1), .Y2(_74ls157_5_y2), .Y3(_74ls157_5_y3), .Y4(_74ls157_5_y4));
  _74LS157 _74ls157_6 (
    .S(nResetP), .A1(1'b0), .A2(PC_FLASH), .A3(PC_FLASH), .A4(1'b0), .B1(DBUS[20]), .B2(DBUS[21]),
    .B3(DBUS[22]), .B4(DBUS[23]), .G(1'b0), .Y1(_74ls157_6_y1), .Y2(_74ls157_6_y2), .Y3(_74ls157_6_y3),
    .Y4(_74ls157_6_y4));
  _74LS163 _74ls163_1 (
    .nPE(and_1_out), .nSR(1'b1), .CP(or_1_out), .CET(1'b1), .CEP(1'b1), .P0(_74ls157_1_y1),
    .P1(_74ls157_1_y2), .P2(_74ls157_1_y3), .P3(_74ls157_1_y4), .TC(_74ls163_1_tc), .Q0(PCbit0),
    .Q1(SPY_PC[1]), .Q2(SPY_PC[2]), .Q3(SPY_PC[3]));
  _74LS163 _74ls163_2 (
    .nPE(and_1_out), .nSR(1'b1), .CP(or_1_out), .CET(_74ls163_1_tc), .CEP(1'b1), .P0(_74ls157_2_y1),
    .P1(_74ls157_2_y2), .P2(_74ls157_2_y3), .P3(_74ls157_2_y4), .TC(_74ls163_2_tc), .Q0(SPY_PC[4]),
    .Q1(SPY_PC[5]), .Q2(SPY_PC[6]), .Q3(SPY_PC[7]));
  _74LS163 _74ls163_3 (
    .nPE(and_1_out), .nSR(1'b1), .CP(or_1_out), .CET(_74ls163_2_tc), .CEP(1'b1), .P0(_74ls157_3_y1),
    .P1(_74ls157_3_y2), .P2(_74ls157_3_y3), .P3(_74ls157_3_y4), .TC(_74ls163_3_tc), .Q0(SPY_PC[8]),
    .Q1(SPY_PC[9]), .Q2(SPY_PC[10]), .Q3(SPY_PC[11]));
  _74LS163 _74ls163_4 (
    .nPE(and_1_out), .nSR(1'b1), .CP(or_1_out), .CET(_74ls163_3_tc), .CEP(1'b1), .P0(_74ls157_4_y1),
    .P1(_74ls157_4_y2), .P2(_74ls157_4_y3), .P3(_74ls157_4_y4), .TC(_74ls163_4_tc), .Q0(SPY_PC[12]),
    .Q1(SPY_PC[13]), .Q2(SPY_PC[14]), .Q3(SPY_PC[15]));
  _74LS163 _74ls163_5 (
    .nPE(and_1_out), .nSR(1'b1), .CP(or_1_out), .CET(_74ls163_4_tc), .CEP(1'b1), .P0(_74ls157_5_y1),
    .P1(_74ls157_5_y2), .P2(_74ls157_5_y3), .P3(_74ls157_5_y4), .TC(_74ls163_5_tc), .Q0(SPY_PC[16]),
    .Q1(SPY_PC[17]), .Q2(SPY_PC[18]), .Q3(SPY_PC[19]));
  _74LS163 _74ls163_6 (
    .nPE(and_1_out), .nSR(1'b1), .CP(or_1_out), .CET(_74ls163_5_tc), .CEP(1'b1), .P0(_74ls157_6_y1),
    .P1(_74ls157_6_y2), .P2(_74ls157_6_y3), .P3(_74ls157_6_y4), .TC(_74ls163_6_tc), .Q0(SPY_PC[20]),
    .Q1(SPY_PC[21]), .Q2(SPY_PC[22]), .Q3(PC_neg));
  // _74LS245 _74ls245_1: pin names not known; wires that end beside it: 1'b1, nE_PC
  // _74LS245 _74ls245_2: pin names not known; wires that end beside it: 1'b1, nE_PC
  // _74LS245 _74ls245_3: pin names not known; wires that end beside it: 1'b1, nE_PC

  assign {SPY_PC[23], SPY_PC[0]} = {PC_neg, PCbit0};

  // Other names for the same wires on the sheet: PCneg = PC_neg

  // Notes on the sheet:
  //   PROGRAM COUNTER
  //   ~Reset
  //   Flash
  //   ~OE
  //   ~LD
  //   CK
  //   NewPC
  //   Neg
  //   Q
endmodule
