// Digital circuit SUBLEQ24-SERIAL.dig as structural Verilog
module SUBLEQ24_SERIAL (
  input  [23:0] DBUS,
  input  nReset,
  input  UARTtxdWrite,
  input  nUARTbusyRead,
  input  nUARTavailRead,
  input  nUARTrxdRead,
  input  BAUDCLK,
  output [23:0] DBUS0
);

  wire _74ls151_1_y, _74ls165_1_qh, _74ls393_1__1qd, _74ls393_1__2qa, _74ls393_1__2qd, _74ls393_2__1qd,
       _74ls393_2__2qb, _74ls393_2__2qd, and_1_out, half7474_1_nq, half7474_3_nq, nand_1_out, nand_2_out,
       nand_3_out, nand_4_out, nand_5_out, nand_6_out, nand_7_out, nand_8_out, nRX_RDY, nTXbusy,
       pulldown_1_out, pullup_1_out, RX, RX_RDY, TX, TXBusy;
  wire [7:0] _74ls564_1_nq7, _74ls595_1_q_a;

  PullUp pullup_1 (.out(pullup_1_out));
  PullDown pulldown_1 (.out(pulldown_1_out));
  Half7474 half7474_1 (.nSD(1'b1), .D(1'b1), .CP(UARTtxdWrite), .nRD(nTXbusy), .nQ(half7474_1_nq));  // open: Q
  _74LS564 _74ls564_1 (
    .nOC(1'b0), .CLK(UARTtxdWrite), .D0(DBUS[0]), .D1(DBUS[1]), .D2(DBUS[2]), .D3(DBUS[3]), .D4(DBUS[4]),
    .D5(DBUS[5]), .D6(DBUS[6]), .D7(DBUS[7]), .nQ0(_74ls564_1_nq7[0]), .nQ1(_74ls564_1_nq7[1]),
    .nQ2(_74ls564_1_nq7[2]), .nQ3(_74ls564_1_nq7[3]), .nQ4(_74ls564_1_nq7[4]), .nQ5(_74ls564_1_nq7[5]),
    .nQ6(_74ls564_1_nq7[6]), .nQ7(_74ls564_1_nq7[7]));
  nand nand_1 (nand_1_out, half7474_1_nq, nReset);
  _74LS393 _74ls393_1 (
    ._1A(BAUDCLK), ._1CL(half7474_3_nq), ._2A(_74ls393_1__1qd), ._2CL(half7474_3_nq), ._1QD(_74ls393_1__1qd),
    ._2QA(_74ls393_1__2qa), ._2QD(_74ls393_1__2qd));  // open: _1QA, _1QB, _1QC, _2QB, _2QC
  // Probe TXCHAR on _74ls564_1_nq7
  nand nand_2 (nand_2_out, _74ls393_1__2qa, _74ls393_1__2qd);
  nand nand_3 (nand_3_out, nand_1_out, nand_1_out);
  Half7474 half7474_2 (.nSD(nand_3_out), .D(1'b1), .CP(1'b1), .nRD(nand_8_out), .Q(TXBusy), .nQ(nTXbusy));
  nand nand_4 (nand_4_out, nand_2_out, nand_2_out);
  nand nand_5 (nand_5_out, _74ls393_1__1qd, nand_4_out);
  Uart_Telnet_GW uart_telnet_gw_1 (.RX(TX), .CLK(BAUDCLK), .TX(RX));
  _74LS393 _74ls393_2 (
    ._1A(BAUDCLK), ._1CL(nTXbusy), ._2A(_74ls393_2__1qd), ._2CL(nTXbusy), ._1QD(_74ls393_2__1qd),
    ._2QB(_74ls393_2__2qb), ._2QD(_74ls393_2__2qd));  // open: _1QA, _1QB, _1QC, _2QA, _2QC
  nand nand_6 (nand_6_out, RX, RX);
  Half7474 half7474_3 (.nSD(RX), .D(1'b0), .CP(nReset), .nRD(nand_5_out), .nQ(half7474_3_nq));  // open: Q
  Half7474 half7474_4 (.nSD(nand_5_out), .D(1'b0), .CP(nReset), .nRD(nUARTrxdRead), .Q(RX_RDY), .nQ(nRX_RDY));
  nand nand_7 (nand_7_out, _74ls393_2__1qd, _74ls393_2__1qd);
  nand nand_8 (nand_8_out, _74ls393_2__2qb, _74ls393_2__2qd);
  _74LS595 _74ls595_1 (
    .SER(nand_6_out), .SCLK(_74ls393_1__1qd), .RCLK(nand_4_out), .nOE(1'b0), .nCLR(nReset),
    .Q_A(_74ls595_1_q_a[7]), .Q_B(_74ls595_1_q_a[6]), .Q_C(_74ls595_1_q_a[5]), .Q_D(_74ls595_1_q_a[4]),
    .Q_E(_74ls595_1_q_a[3]), .Q_F(_74ls595_1_q_a[2]), .Q_G(_74ls595_1_q_a[1]), .Q_H(_74ls595_1_q_a[0]));  // open: Q_H_2
  _74LS165 _74ls165_1 (
    .nLD(half7474_1_nq), .INH(1'b0), .CLK(nand_7_out), .SER(1'b1), .A(1'b1), .B(1'b1), .C(1'b1), .D(1'b1),
    .E(1'b1), .F(1'b1), .G(1'b1), .H(_74ls564_1_nq7[7]), .QH(_74ls165_1_qh));  // open: nQH
  and and_1 (and_1_out, nUARTavailRead, nUARTbusyRead, pullup_1_out);
  _74LS151 _74ls151_1 (
    .A(nUARTavailRead), .B(nUARTbusyRead), .C(pullup_1_out), .S(1'b0), .D0(1'b0), .D1(1'b0), .D2(1'b0),
    .D3(pulldown_1_out), .D4(1'b0), .D5(nTXbusy), .D6(RX_RDY), .D7(1'b0), .Y(_74ls151_1_y));  // open: W
  _74LS541 _74ls541_1 (
    .nOE1(nUARTrxdRead), .nOE2(nUARTrxdRead), ._0D(_74ls595_1_q_a[7]), ._1D(_74ls595_1_q_a[6]),
    ._2D(_74ls595_1_q_a[5]), ._3D(_74ls595_1_q_a[4]), ._4D(_74ls595_1_q_a[3]), ._5D(_74ls595_1_q_a[2]),
    ._6D(_74ls595_1_q_a[1]), ._7D(_74ls595_1_q_a[0]), ._0O(DBUS[7]), ._1O(DBUS[6]), ._2O(DBUS[5]),
    ._3O(DBUS[4]), ._4O(DBUS[3]), ._5O(DBUS[2]), ._6O(DBUS[1]), ._7O(DBUS[0]));
  // Probe RXCHAR on _74ls595_1_q_a
  _74LS541 _74ls541_2 (
    .nOE1(and_1_out), .nOE2(and_1_out), ._0D(_74ls151_1_y), ._1D(1'b0), ._2D(1'b0), ._3D(1'b0), ._4D(1'b0),
    ._5D(1'b0), ._6D(1'b0), ._7D(1'b0), ._0O(DBUS[0]), ._1O(DBUS[1]), ._2O(DBUS[2]), ._3O(DBUS[3]),
    ._4O(DBUS[4]), ._5O(DBUS[5]), ._6O(DBUS[6]), ._7O(DBUS[7]));
  _74LS165 _74ls165_2 (
    .nLD(half7474_1_nq), .INH(1'b0), .CLK(nand_7_out), .SER(_74ls165_1_qh), .A(_74ls564_1_nq7[6]),
    .B(_74ls564_1_nq7[5]), .C(_74ls564_1_nq7[4]), .D(_74ls564_1_nq7[3]), .E(_74ls564_1_nq7[2]),
    .F(_74ls564_1_nq7[1]), .G(_74ls564_1_nq7[0]), .H(1'b0), .QH(TX));  // open: nQH
  // NotConnected on DBUS[23:8]

  assign DBUS0 = DBUS;

  // Other names for the same wires on the sheet: BAUD = BAUDCLK

  // Notes on the sheet:
  //   BAUDCLK: Hz: 153600
  //   UART
  //   ~D
endmodule
