// Digital circuit SUBLEQ24-SUBTRACTOR.dig as structural Verilog
module SUBLEQ24_SUBTRACTOR (
  input  [23:0] DBUS,
  input  nIOwrite,
  input  nResult_E,
  input  Aval_CK,
  input  Bval_CK,
  output [23:0] DBUSo,
  output isLEQ,
  output [23:0] SPY_sub
);

  wire _74ls283_1_p2, _74ls283_2_p2, _74ls283_3_p2, _74ls283_4_p2, _74ls283_5_p2, nand_1_out, nand_2_out,
       nor_1_out, nor_2_out, nor_3_out, nor_4_out, nor_5_out, nor_6_out, nor_7_out, nor_8_out;

  // _74LS564 _74ls564_1: pin names not known; wires that end beside it: 1'b0, Aval_CK
  // _74LS564 _74ls564_2: pin names not known; wires that end beside it: 1'b0, Aval_CK
  // _74LS564 _74ls564_3: pin names not known; wires that end beside it: 1'b0, Aval_CK
  // _74LS574 _74ls574_1: pin names not known; wires that end beside it: 1'b0, Bval_CK
  // _74LS574 _74ls574_2: pin names not known; wires that end beside it: 1'b0, Bval_CK
  // _74LS574 _74ls574_3: pin names not known; wires that end beside it: 1'b0, Bval_CK
  // _74LS283 _74ls283_1: pin names not known; wires that end beside it: nIOwrite, _74ls283_1_p2
  // _74LS283 _74ls283_2: pin names not known; wires that end beside it: _74ls283_1_p2, _74ls283_2_p2
  // _74LS283 _74ls283_3: pin names not known; wires that end beside it: _74ls283_2_p2, _74ls283_3_p2
  // _74LS283 _74ls283_4: pin names not known; wires that end beside it: _74ls283_3_p2, _74ls283_4_p2
  // _74LS283 _74ls283_5: pin names not known; wires that end beside it: _74ls283_4_p2, _74ls283_5_p2
  // _74LS283 _74ls283_6: pin names not known; wires that end beside it: _74ls283_5_p2
  // _74LS245 _74ls245_1: pin names not known; wires that end beside it: 1'b1, nResult_E, DBUSo[0], DBUSo[1], DBUSo[2], DBUSo[3], DBUSo[4], DBUSo[5], DBUSo[6], DBUSo[7]
  // _74LS245 _74ls245_2: pin names not known; wires that end beside it: 1'b1, nResult_E, DBUSo[8], DBUSo[9], DBUSo[10], DBUSo[11], DBUSo[12], DBUSo[13], DBUSo[14], DBUSo[15]
  // _74LS245 _74ls245_3: pin names not known; wires that end beside it: 1'b1, nResult_E, DBUSo[16], DBUSo[17], DBUSo[18], DBUSo[19], DBUSo[20], DBUSo[21], DBUSo[22], DBUSo[23]
  nor nor_1 (nor_1_out, SPY_sub[3], SPY_sub[2], SPY_sub[1]);
  nor nor_2 (nor_2_out, SPY_sub[0], SPY_sub[7], SPY_sub[6]);
  nor nor_3 (nor_3_out, SPY_sub[5], SPY_sub[4], SPY_sub[11]);
  nor nor_4 (nor_4_out, SPY_sub[10], SPY_sub[9], SPY_sub[8]);
  nor nor_5 (nor_5_out, SPY_sub[15], SPY_sub[14], SPY_sub[13]);
  nor nor_6 (nor_6_out, SPY_sub[12], SPY_sub[19], SPY_sub[18]);
  nor nor_7 (nor_7_out, SPY_sub[17], SPY_sub[16], SPY_sub[23]);
  nor nor_8 (nor_8_out, SPY_sub[22], SPY_sub[21], SPY_sub[20]);
  nand nand_1 (nand_1_out, nor_1_out, nor_2_out, nor_3_out, nor_4_out, nor_5_out, nor_6_out, nor_7_out, nor_8_out);
  nand nand_2 (nand_2_out, SPY_sub[23], SPY_sub[23]);
  nand nand_3 (isLEQ, nand_2_out, nand_1_out);

  // Notes on the sheet:
  //   LATCHED SUBTRACTOR
  //   Out Enable
  //   Carry In
endmodule
