// Digital circuit SUBLEQ24-backup.dig as structural Verilog
module SUBLEQ24_backup (
  input  XTAL,
  input  TraceClock,
  input  TRACE,
  input  [7:0] GPIO2in,
  input  in_5,
  input  in_6,
  input  in_7,
  input  in_8,
  input  in_9,
  input  in_10,
  input  in_11,
  input  in_12,
  input  in_13,
  input  in_14,
  input  in_15,
  input  in_16,
  input  in_17,
  input  clk,
  input  clk_2
);

  wire _74ls138_1_ny0, _74ls138_1_ny1, _74ls138_1_ny2, _74ls138_1_ny3, _74ls138_1_ny4, _74ls138_1_ny5,
       _74ls138_1_ny6, _74ls138_1_ny7, _74ls151_1_y, _74ls157_1_y1, _74ls157_1_y2, _74ls157_1_y3,
       _74ls157_1_y4, _74ls157_2_y1, _74ls157_2_y2, _74ls157_2_y3, _74ls157_2_y4, _74ls157_3_y1,
       _74ls157_3_y2, _74ls157_3_y3, _74ls157_3_y4, _74ls157_4_y1, _74ls157_4_y2, _74ls157_4_y3,
       _74ls157_4_y4, _74ls157_5_y1, _74ls157_5_y2, _74ls157_5_y3, _74ls157_5_y4, _74ls157_6_y1,
       _74ls157_6_y2, _74ls157_6_y3, _74ls157_6_y4, _74ls163_2_tc, _74ls163_3_tc, _74ls163_4_tc,
       _74ls163_5_tc, _74ls163_6_tc, _74ls163_7_tc, _74ls165_1_qh, _74ls175_1_p3, _74ls175_1_p4,
       _74ls175_1_p5, _74ls175_1_p6, _74ls175_2_p3, _74ls175_2_p4, _74ls175_2_p5, _74ls175_2_p6,
       _74ls238_1_y0, _74ls238_1_y1, _74ls238_1_y2, _74ls238_1_y3, _74ls238_1_y4, _74ls238_1_y5,
       _74ls238_1_y6, _74ls238_1_y7, _74ls238_2_y0, _74ls238_2_y1, _74ls238_2_y2, _74ls238_2_y3,
       _74ls238_2_y4, _74ls238_2_y5, _74ls238_2_y6, _74ls238_2_y7, _74ls283_1_p2, _74ls283_2_p2,
       _74ls283_3_p2, _74ls283_4_p2, _74ls283_5_p2, _74ls393_1__1qd, _74ls393_1__2qa, _74ls393_1__2qd,
       _74ls393_2__1qd, _74ls393_2__2qb, _74ls393_2__2qd, A, AisNeg, and_2_out, and_3_out, and_4_out,
       and_5_out, and_6_out, and_27_out, and_28_out, and_29_out, and_30_out, and_31_out, and_32_out,
       and_33_out, and_34_out, and_35_out, B, BisNeg, C, d_ff_1_q, d_ff_2_q, delay_1_out, delay_2_out,
       delay_3_out, delay_4_out, DMA, half7474_1_q, half7474_2_q, half7474_3_q, half7474_4_q, half7474_5_nq,
       half7474_6_nq, half7474_7_nq, half7474_8_nq, half7474_11_nq, half7474_11_q, half7474_12_q,
       half7474_13_q, half7474_14_nq, half7474_17_nq, half7474_19_nq, half7474_21_q, half7474_22_q,
       half7474_24_q, half7474_25_q, half7474_26_q, half7474_27_nq, half7474_28_nq, INTA_CK, INTREQ, IOread,
       IOrw, IOwrite, isLEQ, M_out, nand_1_out, nand_2_out, nand_3_out, nand_4_out, nand_6_out, nand_7_out,
       nand_8_out, nand_9_out, nand_10_out, nand_11_out, nand_12_out, nand_13_out, nCK, nE_PC, nINTA_E,
       nIOread, nIOreadP, nIOwrite, nIOwriteP, nMAR_E, noIO, nor_1_out, nor_2_out, nor_3_out, nor_4_out,
       nor_5_out, nor_6_out, nor_7_out, nor_8_out, nor_9_out, nor_10_out, nor_12_out, not_2_out, not_4_out,
       not_6_out, not_9_out, not_10_out, not_11_out, not_12_out, not_13_out, not_14_out, not_15_out,
       not_24_out, not_25_out, nPC_LD, nRD, nReset, nResetP, nResult_E, nRX_RDY, nTXbusy, nWR, or_2_out,
       or_3_out, or_4_out, or_5_out, or_6_out, or_9_out, or_10_out, or_11_out, or_12_out, or_13_out,
       or_14_out, PC_FLASH, PCbit0, PCneg, POR, pulldown_1_out, pulldown_39_out, pullup_2_out, R_out, Reset,
       RUN, RX, RX_RDY, S_out, Tick, TS0, TS1, TS2, TS3, TS3io, TS3ior, TS3iow, TS3noio, TS4, TS4io, TS4ior,
       TS4iow, TS4noio, TS5, TS5io, TS5ior, TS5iow, TS5noio, TS6, TS6io, TS6ior, TS6iow, TS6noio, TS7, TS7io,
       TS7ior, TS7iow, TS7noio, TX, TXBusy, xor_1_out, Z_out;
  wire [3:0] pulldown_3_out_2, pulldown_3_out_3, pulldown_4_out, pulldown_4_out_2;
  wire [7:0] _74ls564_5_nq0, _74ls595_1_q_a, undriven, undriven_2, undriven_3, undriven_4;
  wire [19:0] counter_1_out, d_ff_4_q;
  wire [22:1] SPY_PC;
  wire [23:0] ABUS, d_ff_5_q, DBUS, not_7_out, not_8_out, ramasync_1_q, SPY_sub;
  wire [23:8] pulldown_3_out, pulldown_4_out_3;

  D_FF d_ff_1 (.D(1'b1), .C(TraceClock), .Q(d_ff_1_q));  // open: nQ
  // And and_1 has open pins: In_1=PCneg, In_2=PCbit0, out=open
  D_FF d_ff_2 (.D(d_ff_1_q), .C(TraceClock), .Q(d_ff_2_q));  // open: nQ
  Button F (.out(PC_FLASH));
  Button Z (.out(Z_out));
  Button M (.out(M_out));
  Button R (.out(R_out));
  Button S (.out(S_out));
  D_FF d_ff_3 (.D(d_ff_2_q), .C(TraceClock), .nQ(POR));  // open: Q
  or or_1 (Reset, PC_FLASH, POR, Z_out);
  and and_2 (and_2_out, TRACE, TraceClock);
  Counter #(.Bits(20)) counter_1 (.en(1'b1), .C(TS0), .clr(clk), .out(counter_1_out));  // open: ovf
  PullDown pulldown_1 (.out(pulldown_1_out));
  or or_2 (or_2_out, R_out, S_out, and_2_out);
  D_FF #(.Bits(20)) d_ff_4 (.D(counter_1_out), .C(clk), .Q(d_ff_4_q));  // open: nQ
  not not_1 (nReset, Reset);
  Half7474 half7474_1 (.nSD(1'b1), .D(Reset), .CP(XTAL), .nRD(1'b1), .Q(half7474_1_q));  // open: nQ
  Half7474 half7474_2 (.nSD(1'b1), .D(pulldown_1_out), .CP(XTAL), .nRD(nResetP), .Q(half7474_2_q));  // open: nQ
  Half7474 half7474_3 (.nSD(1'b1), .D(R_out), .CP(XTAL), .nRD(nResetP), .Q(half7474_3_q));  // open: nQ
  Half7474 half7474_4 (.nSD(1'b1), .D(or_2_out), .CP(XTAL), .nRD(nResetP), .Q(half7474_4_q));  // open: nQ
  // Probe on d_ff_4_q
  or or_3 (or_3_out, nWR, POR);
  not not_2 (not_2_out, TS0);
  Half7474 half7474_5 (.nSD(1'b1), .D(half7474_1_q), .CP(XTAL), .nRD(1'b1), .nQ(half7474_5_nq));  // open: Q
  Half7474 half7474_6 (.nSD(1'b1), .D(half7474_2_q), .CP(XTAL), .nRD(nResetP), .nQ(half7474_6_nq));  // open: Q
  Half7474 half7474_7 (.nSD(1'b1), .D(half7474_3_q), .CP(XTAL), .nRD(nResetP), .nQ(half7474_7_nq));  // open: Q
  Half7474 half7474_8 (.nSD(1'b1), .D(half7474_4_q), .CP(XTAL), .nRD(nResetP), .nQ(half7474_8_nq));  // open: Q
  not not_3 (nCK, XTAL);
  // Probe on ABUS
  not not_4 (not_4_out, TS0);
  and and_3 (and_3_out, half7474_1_q, half7474_5_nq);
  and and_4 (and_4_out, half7474_2_q, half7474_6_nq);
  and and_5 (and_5_out, half7474_3_q, half7474_7_nq);
  and and_6 (and_6_out, half7474_4_q, half7474_8_nq);
  RAMAsync #(.AddrBits(24), .isProgramMemory("true"), .Bits(24)) ramasync_1 (
    .A(ABUS), .D(DBUS), .we(~or_3_out), .Q(ramasync_1_q));
  or or_4 (or_4_out, ~or_3_out, nRD);  // Or
  // _74LS574 _74ls574_1: pin names not known; wires that end beside it: nMAR_E, in_5
  // _74LS574 _74ls574_2: pin names not known; wires that end beside it: nMAR_E, in_5
  // _74LS574 _74ls574_3: pin names not known; wires that end beside it: nMAR_E, in_5
  Half7474 half7474_9 (.nSD(1'b1), .D(DBUS[23]), .CP(in_6), .nRD(not_2_out), .Q(AisNeg));  // open: nQ
  Half7474 half7474_10 (.nSD(1'b1), .D(DBUS[23]), .CP(in_7), .nRD(not_4_out), .Q(BisNeg));  // open: nQ
  not not_5 (nResetP, and_3_out);
  or or_5 (or_5_out, and_4_out, and_5_out);
  not not_6 (not_6_out, and_6_out);
  PullUp #(.Bits(24)) pullup_1 ();  // open: out
  // Probe on DBUS
  assign DBUS = ~or_4_out ? ramasync_1_q : 24'bz;  // DriverInvSel driverinvsel_1
  PullDown #(.Bits(24)) pulldown_2 (.out(DBUS));
  Half7474 half7474_11 (
    .nSD(1'b1), .D(half7474_11_nq), .CP(or_5_out), .nRD(nResetP), .Q(half7474_11_q), .nQ(half7474_11_nq));
  Half7474 half7474_12 (.nSD(not_6_out), .D(1'b0), .CP(TS6), .nRD(nResetP), .Q(half7474_12_q));  // open: nQ
  // Probe on in_5
  or or_6 (or_6_out, half7474_11_q, half7474_12_q);
  // _74LS564 _74ls564_1: pin names not known; wires that end beside it: 1'b0, in_14
  // _74LS564 _74ls564_2: pin names not known; wires that end beside it: 1'b0, in_14
  // _74LS564 _74ls564_3: pin names not known; wires that end beside it: 1'b0, in_14
  // _74LS574 _74ls574_4: pin names not known; wires that end beside it: 1'b0, in_15
  // _74LS574 _74ls574_5: pin names not known; wires that end beside it: 1'b0, in_15
  // _74LS574 _74ls574_6: pin names not known; wires that end beside it: 1'b0, in_15
  Half7474 half7474_13 (.nSD(1'b1), .D(M_out), .CP(nCK), .nRD(nResetP), .Q(half7474_13_q));  // open: nQ
  Half7474 half7474_14 (.nSD(1'b1), .D(or_6_out), .CP(nCK), .nRD(nResetP), .Q(RUN), .nQ(half7474_14_nq));
  // Probe PROGRAM COUNTER on {PCneg, SPY_PC, PCbit0}
  // Probe SUBTRACTOR on SPY_sub
  D_FF #(.Bits(24)) d_ff_5 (.D(DBUS), .C(in_5), .Q(d_ff_5_q));  // open: nQ
  // Probe MAR on d_ff_5_q
  LED u_RUN (.in(RUN));
  PullDown #(.Bits(24)) pulldown_3 (.out({pulldown_3_out, pulldown_3_out_3, pulldown_3_out_2}));
  PullDown #(.Bits(24)) pulldown_4 (.out({pulldown_4_out_3, pulldown_4_out_2, pulldown_4_out}));
  nor nor_1 (nor_1_out, half7474_14_nq, nCK);
  // Probe on nor_1_out
  assign not_7_out = ~SPY_sub;  // Not not_7, 24 bits wide
  assign not_8_out = ~{pulldown_3_out, pulldown_3_out_3, pulldown_3_out_2};  // Not not_8, 24 bits wide
  nor nor_2 (nor_2_out, Reset, TS6);
  or or_7 (Tick, and_3_out, half7474_13_q, nor_1_out);
  not not_9 (not_9_out, DMA);
  // Probe ~SUBTRACTOR on not_7_out
  // Probe ~AVAL on not_8_out
  // Probe BVAL on {pulldown_4_out_3, pulldown_4_out_2, pulldown_4_out}
  // Probe on Tick
  // _74LS283 _74ls283_1: pin names not known; wires that end beside it: nIOwrite, _74ls283_1_p2
  _74LS163 _74ls163_1 (
    .nPE(nor_2_out), .nSR(1'b1), .CP(Tick), .CET(1'b1), .CEP(not_9_out), .P0(1'b0), .P1(1'b0), .P2(1'b0),
    .P3(1'b0), .Q0(A), .Q1(B), .Q2(C));  // open: TC, Q3
  // _74LS283 _74ls283_2: pin names not known; wires that end beside it: _74ls283_1_p2, _74ls283_2_p2
  nor nor_3 (nor_3_out, SPY_sub[2], SPY_sub[1], SPY_sub[0]);
  nor nor_4 (nor_4_out, SPY_sub[5], SPY_sub[4], SPY_sub[3]);
  // Probe on C
  nor nor_5 (nor_5_out, SPY_sub[8], SPY_sub[7], SPY_sub[6]);
  nor nor_6 (nor_6_out, SPY_sub[11], SPY_sub[10], SPY_sub[9]);
  Delay #(.delayTime(10)) delay_1 (.in(not_10_out), .out(delay_1_out));
  not not_10 (not_10_out, Tick);
  not not_11 (not_11_out, nReset);
  Delay #(.delayTime(10)) delay_2 (.in(not_11_out), .out(delay_2_out));
  and and_7 (TS3ior, TS3, IOread);
  and and_8 (TS4ior, TS4, IOread);
  and and_9 (TS5ior, TS5, IOread);
  and and_10 (TS6ior, TS6, IOread);
  and and_11 (TS7ior, TS7, IOread);
  nand nand_1 (nand_1_out, TS3, BisNeg);
  not not_12 (not_12_out, TS0);
  nand nand_2 (nand_2_out, TS1, AisNeg);
  not not_13 (not_13_out, TS0);
  LED led_1 (.in(TS0));
  // _74LS283 _74ls283_3: pin names not known; wires that end beside it: _74ls283_2_p2, _74ls283_3_p2
  nor nor_7 (nor_7_out, SPY_sub[14], SPY_sub[13], SPY_sub[12]);
  nor nor_8 (nor_8_out, SPY_sub[17], SPY_sub[16], SPY_sub[15]);
  nand nand_3 (nand_3_out, nor_10_out, nor_9_out, nor_8_out, nor_7_out, nor_6_out, nor_5_out, nor_4_out, nor_3_out);
  xor xor_1 (xor_1_out, delay_1_out, delay_2_out);
  LED led_2 (.in(TS1));
  nor nor_9 (nor_9_out, SPY_sub[20], SPY_sub[19], SPY_sub[18]);
  _74LS238 _74ls238_1 (
    .A(A), .B(B), .C(C), .G(nReset), .nGA(DMA), .nGB(1'b0), .Y0(_74ls238_1_y0), .Y1(_74ls238_1_y1),
    .Y2(_74ls238_1_y2), .Y3(_74ls238_1_y3), .Y4(_74ls238_1_y4), .Y5(_74ls238_1_y5), .Y6(_74ls238_1_y6),
    .Y7(_74ls238_1_y7));
  Half7474 half7474_15 (.nSD(nand_1_out), .D(1'b0), .CP(nResetP), .nRD(not_12_out), .Q(IOwrite), .nQ(nIOwrite));
  Half7474 half7474_16 (.nSD(nand_2_out), .D(1'b0), .CP(nResetP), .nRD(not_13_out), .Q(IOread), .nQ(nIOread));
  LED led_3 (.in(TS2));
  // _74LS283 _74ls283_4: pin names not known; wires that end beside it: _74ls283_3_p2, _74ls283_4_p2
  nor nor_10 (nor_10_out, SPY_sub[23], SPY_sub[22], SPY_sub[21]);
  and and_12 (TS3iow, TS3, IOwrite);
  and and_13 (TS4iow, TS4, IOwrite);
  and and_14 (TS5iow, TS5, IOwrite);
  and and_15 (TS6iow, TS6, IOwrite);
  and and_16 (TS7iow, TS7, IOwrite);
  LightBulb lightbulb_1 (.A(IOwrite), .B(1'b0));
  LightBulb lightbulb_2 (.A(IOread), .B(1'b0));
  LED led_4 (.in(TS3));
  LED led_5 (.in(TS4));
  LED led_6 (.in(TS3noio));
  LED led_7 (.in(TS4noio));
  LED led_8 (.in(TS3io));
  LED led_9 (.in(TS4io));
  LED led_10 (.in(TS3ior));
  LED led_11 (.in(TS4ior));
  LED led_12 (.in(TS3iow));
  LED led_13 (.in(TS4iow));
  _74LS574 _74ls574_7 (
    .nOC(DMA), .CLK(xor_1_out), .D0(_74ls238_1_y0), .D1(_74ls238_1_y1), .D2(_74ls238_1_y2),
    .D3(_74ls238_1_y3), .D4(_74ls238_1_y4), .D5(_74ls238_1_y5), .D6(_74ls238_1_y6), .D7(_74ls238_1_y7),
    .Q0(TS0), .Q1(TS1), .Q2(TS2), .Q3(TS3), .Q4(TS4), .Q5(TS5), .Q6(TS6), .Q7(TS7));
  // Probe on IOwrite
  // Probe on IOread
  LED led_14 (.in(TS5));
  LED led_15 (.in(TS5noio));
  LED led_16 (.in(TS5io));
  LED led_17 (.in(TS5ior));
  LED led_18 (.in(TS5iow));
  PullDown pulldown_5 (.out(TS0));
  PullDown pulldown_6 (.out(TS1));
  and and_17 (TS3io, TS3, IOrw);
  and and_18 (TS4io, TS4, IOrw);
  and and_19 (TS5io, TS5, IOrw);
  and and_20 (TS6io, TS6, IOrw);
  and and_21 (TS7io, TS7, IOrw);
  not not_14 (not_14_out, TS3ior);
  LED led_19 (.in(TS6));
  LED led_20 (.in(TS6noio));
  LED led_21 (.in(TS6io));
  LED led_22 (.in(TS6ior));
  LED led_23 (.in(TS6iow));
  // _74LS283 _74ls283_5: pin names not known; wires that end beside it: _74ls283_4_p2, _74ls283_5_p2
  PullDown pulldown_7 (.out(TS2));
  PullDown pulldown_8 (.out(TS3));
  PullDown pulldown_9 (.out(TS4));
  PullDown pulldown_10 (.out(TS5));
  not not_15 (not_15_out, not_14_out);
  not not_16 (nIOreadP, not_15_out);
  Delay #(.delayTime(20)) delay_3 (.in(TS4iow), .out(delay_3_out));
  not not_17 (nIOwriteP, delay_3_out);
  or or_8 (IOrw, IOwrite, IOread);
  nor nor_11 (noIO, IOwrite, IOread);
  LED led_24 (.in(TS7));
  LED led_25 (.in(TS7noio));
  LED led_26 (.in(TS7io));
  LED led_27 (.in(TS7ior));
  LED led_28 (.in(TS7iow));
  PullDown pulldown_11 (.out(TS6));
  PullDown pulldown_12 (.out(TS7));
  // _74LS283 _74ls283_6: pin names not known; wires that end beside it: _74ls283_5_p2
  nand nand_4 (nand_4_out, SPY_sub[23], SPY_sub[23]);
  and and_22 (TS3noio, TS3, noIO);
  and and_23 (TS4noio, TS4, noIO);
  and and_24 (TS5noio, TS5, noIO);
  and and_25 (TS6noio, TS6, noIO);
  and and_26 (TS7noio, TS7, noIO);
  nand nand_5 (isLEQ, nand_4_out, nand_3_out);
  _74LS245 _74ls245_1 (
    .DIR(1'b1), .A1(SPY_sub[0]), .A2(SPY_sub[1]), .A3(SPY_sub[2]), .A4(SPY_sub[3]), .A5(SPY_sub[4]),
    .A6(SPY_sub[5]), .A7(SPY_sub[6]), .A8(SPY_sub[7]), .nOE(nResult_E), .B1(DBUS[0]), .B2(DBUS[1]),
    .B3(DBUS[2]), .B4(DBUS[3]), .B5(DBUS[4]), .B6(DBUS[5]), .B7(DBUS[6]), .B8(DBUS[7]));
  _74LS245 _74ls245_2 (
    .DIR(1'b1), .A1(SPY_sub[8]), .A2(SPY_sub[9]), .A3(SPY_sub[10]), .A4(SPY_sub[11]), .A5(SPY_sub[12]),
    .A6(SPY_sub[13]), .A7(SPY_sub[14]), .A8(SPY_sub[15]), .nOE(nResult_E), .B1(DBUS[8]), .B2(DBUS[9]),
    .B3(DBUS[10]), .B4(DBUS[11]), .B5(DBUS[12]), .B6(DBUS[13]), .B7(DBUS[14]), .B8(DBUS[15]));
  _74LS245 _74ls245_3 (
    .DIR(1'b1), .A1(SPY_sub[16]), .A2(SPY_sub[17]), .A3(SPY_sub[18]), .A4(SPY_sub[19]), .A5(SPY_sub[20]),
    .A6(SPY_sub[21]), .A7(SPY_sub[22]), .A8(SPY_sub[23]), .nOE(nResult_E), .B1(DBUS[16]), .B2(DBUS[17]),
    .B3(DBUS[18]), .B4(DBUS[19]), .B5(DBUS[20]), .B6(DBUS[21]), .B7(DBUS[22]), .B8(DBUS[23]));
  LED led_29 (.in(in_11));
  LED led_30 (.in(in_13));
  LED led_31 (.in(in_5));
  LED led_32 (.in(in_6));
  LED led_33 (.in(in_7));
  LED led_34 (.in(in_9));
  LED led_35 (.in(in_14));
  LED led_36 (.in(in_15));
  LED led_37 (.in(in_8));
  LED led_38 (.in(in_12));
  LED led_39 (.in(in_16));
  LED led_40 (.in(in_10));
  LED led_41 (.in(isLEQ));
  LED led_42 (.in(AisNeg));
  LED led_43 (.in(BisNeg));
  and and_27 (and_27_out, TS3, ~IOread);  // And
  or or_9 (or_9_out, TS0, TS2, TS5);
  or or_10 (or_10_out, TS0, TS1, TS2, and_27_out, TS5);
  or or_11 (or_11_out, TS1, TS3);
  or or_12 (or_12_out, TS1, TS3, TS4);
  or or_13 (or_13_out, TS1, TS3, TS6);
  and and_28 (and_28_out, TS4, nIOwrite);
  and and_29 (and_29_out, TS5, nIOwrite, isLEQ);
  PullDown pulldown_13 (.out(or_12_out));
  PullDown pulldown_14 (.out(or_13_out));
  PullDown pulldown_15 (.out(and_28_out));
  PullDown pulldown_16 (.out(TS4));
  PullDown pulldown_17 (.out(TS6));
  // Probe on nIOwriteP
  // Probe on nIOreadP
  assign in_11 = or_9_out ? 1'b1 : 1'bz;  // Driver driver_1
  PullDown pulldown_18 (.out(or_9_out));
  assign in_13 = or_10_out ? 1'b1 : 1'bz;  // Driver driver_2
  PullDown pulldown_19 (.out(or_10_out));
  assign in_5 = or_11_out ? 1'b1 : 1'bz;  // Driver driver_3
  PullDown pulldown_20 (.out(or_11_out));
  assign in_6 = TS1 ? 1'b1 : 1'bz;  // Driver driver_4
  PullDown pulldown_21 (.out(TS1));
  assign in_7 = TS3 ? 1'b1 : 1'bz;  // Driver driver_5
  PullDown pulldown_22 (.out(TS3));
  assign in_9 = or_12_out ? 1'b1 : 1'bz;  // Driver driver_6
  assign in_14 = TS2 ? 1'b1 : 1'bz;  // Driver driver_7
  PullDown pulldown_23 (.out(TS2));
  assign in_15 = TS4 ? 1'b1 : 1'bz;  // Driver driver_8
  PullDown pulldown_24 (.out(TS4));
  assign in_8 = or_13_out ? 1'b1 : 1'bz;  // Driver driver_9
  assign in_12 = and_28_out ? 1'b1 : 1'bz;  // Driver driver_10
  assign in_16 = TS4 ? 1'b1 : 1'bz;  // Driver driver_11
  assign in_10 = and_29_out ? 1'b1 : 1'bz;  // Driver driver_12
  PullDown pulldown_25 (.out(and_29_out));
  assign in_17 = TS6 ? 1'b1 : 1'bz;  // Driver driver_13
  // _74LS175 _74ls175_1: pin names not known; wires that end beside it: in_7, 1'b1, _74ls175_1_p3, _74ls175_1_p4, _74ls175_1_p5, _74ls175_1_p6
  // _74LS175 _74ls175_2: pin names not known; wires that end beside it: in_6, 1'b1, _74ls175_2_p3, _74ls175_2_p4, _74ls175_2_p5, _74ls175_2_p6
  _74LS238 _74ls238_2 (
    .A(_74ls175_1_p3), .B(_74ls175_1_p4), .C(_74ls175_1_p5), .G(1'b1), .nGA(_74ls175_1_p6), .nGB(nIOwriteP),
    .Y0(_74ls238_2_y0), .Y1(_74ls238_2_y1), .Y2(_74ls238_2_y2), .Y3(_74ls238_2_y3), .Y4(_74ls238_2_y4),
    .Y5(_74ls238_2_y5), .Y6(_74ls238_2_y6), .Y7(_74ls238_2_y7));
  _74LS138 _74ls138_1 (
    .A(_74ls175_2_p3), .B(_74ls175_2_p4), .C(_74ls175_2_p5), .G(1'b1), .nGB(_74ls175_2_p6), .nGA(nIOreadP),
    .nY0(_74ls138_1_ny0), .nY1(_74ls138_1_ny1), .nY2(_74ls138_1_ny2), .nY3(_74ls138_1_ny3),
    .nY4(_74ls138_1_ny4), .nY5(_74ls138_1_ny5), .nY6(_74ls138_1_ny6), .nY7(_74ls138_1_ny7));
  // Probe on nIOreadP
  PullDown pulldown_26 (.out(in_5));
  PullDown pulldown_27 (.out(in_6));
  PullDown pulldown_28 (.out(in_7));
  PullDown pulldown_29 (.out(in_9));
  PullDown pulldown_30 (.out(in_8));
  PullDown pulldown_31 (.out(in_10));
  PullDown pulldown_32 (.out(in_11));
  PullDown pulldown_33 (.out(in_12));
  PullDown pulldown_34 (.out(in_13));
  PullDown pulldown_35 (.out(in_14));
  PullDown pulldown_36 (.out(in_15));
  PullDown pulldown_37 (.out(in_16));
  PullDown pulldown_38 (.out(in_17));
  _74LS541 _74ls541_1 (
    .nOE1(_74ls138_1_ny4), .nOE2(_74ls138_1_ny4), ._0D(GPIO2in[0]), ._1D(GPIO2in[1]), ._2D(GPIO2in[2]),
    ._3D(GPIO2in[3]), ._4D(GPIO2in[4]), ._5D(GPIO2in[5]), ._6D(GPIO2in[6]), ._7D(GPIO2in[7]), ._0O(DBUS[0]),
    ._1O(DBUS[1]), ._2O(DBUS[2]), ._3O(DBUS[3]), ._4O(DBUS[4]), ._5O(DBUS[5]), ._6O(DBUS[6]), ._7O(DBUS[7]));
  _74LS541 _74ls541_2 (
    .nOE1(nIOreadP), .nOE2(nIOreadP), ._0D(1'b0), ._1D(1'b0), ._2D(1'b0), ._3D(1'b0), ._4D(1'b0), ._5D(1'b0),
    ._6D(1'b0), ._7D(1'b0), ._0O(DBUS[8]), ._1O(DBUS[9]), ._2O(DBUS[10]), ._3O(DBUS[11]), ._4O(DBUS[12]),
    ._5O(DBUS[13]), ._6O(DBUS[14]), ._7O(DBUS[15]));
  _74LS541 _74ls541_3 (
    .nOE1(nIOreadP), .nOE2(nIOreadP), ._0D(1'b0), ._1D(1'b0), ._2D(1'b0), ._3D(1'b0), ._4D(1'b0), ._5D(1'b0),
    ._6D(1'b0), ._7D(1'b0), ._0O(DBUS[16]), ._1O(DBUS[17]), ._2O(DBUS[18]), ._3O(DBUS[19]), ._4O(DBUS[20]),
    ._5O(DBUS[21]), ._6O(DBUS[22]), ._7O(DBUS[23]));
  not not_18 (nMAR_E, in_9);
  not not_19 (nPC_LD, in_10);
  not not_20 (nE_PC, in_11);
  not not_21 (nWR, in_12);
  not not_22 (nRD, in_13);
  not not_23 (nResult_E, in_16);
  // Probe on _74ls238_2_y0
  // Probe on _74ls238_2_y1
  // Probe on _74ls238_2_y2
  // Probe on _74ls238_2_y3
  // Probe on _74ls238_2_y4
  // Probe on _74ls238_2_y5
  // Probe on _74ls238_2_y6
  // Probe on _74ls238_2_y7
  // Probe on _74ls138_1_ny0
  // Probe on _74ls138_1_ny1
  // Probe on _74ls138_1_ny2
  // Probe on _74ls138_1_ny3
  // Probe on _74ls138_1_ny4
  // Probe on _74ls138_1_ny5
  // Probe on _74ls138_1_ny6
  // Probe on _74ls138_1_ny7
  // _74LS564 _74ls564_4: pin names not known; wires that end beside it: 1'b0, _74ls238_2_y4
  // Probe on undriven
  PullUp pullup_2 (.out(pullup_2_out));
  PullDown pulldown_39 (.out(pulldown_39_out));
  Uart_Telnet_GW uart_telnet_gw_1 (.RX(TX), .CLK(clk_2), .TX(RX));
  Half7474 half7474_17 (.nSD(1'b1), .D(1'b1), .CP(_74ls238_2_y7), .nRD(nTXbusy), .nQ(half7474_17_nq));  // open: Q
  _74LS564 _74ls564_5 (
    .nOC(1'b0), .CLK(_74ls238_2_y7), .D0(DBUS[0]), .D1(DBUS[1]), .D2(DBUS[2]), .D3(DBUS[3]), .D4(DBUS[4]),
    .D5(DBUS[5]), .D6(DBUS[6]), .D7(DBUS[7]), .nQ0(_74ls564_5_nq0[0]), .nQ1(_74ls564_5_nq0[1]),
    .nQ2(_74ls564_5_nq0[2]), .nQ3(_74ls564_5_nq0[3]), .nQ4(_74ls564_5_nq0[4]), .nQ5(_74ls564_5_nq0[5]),
    .nQ6(_74ls564_5_nq0[6]), .nQ7(_74ls564_5_nq0[7]));  // open: nSPY, SPY
  _74LS393 _74ls393_1 (
    ._1A(clk_2), ._1CL(half7474_19_nq), ._2A(_74ls393_1__1qd), ._2CL(half7474_19_nq), ._1QD(_74ls393_1__1qd),
    ._2QA(_74ls393_1__2qa), ._2QD(_74ls393_1__2qd));  // open: _1QA, _1QB, _1QC, _2QB, _2QC
  nand nand_6 (nand_6_out, half7474_17_nq, nReset);
  // Probe TXCHAR on _74ls564_5_nq0
  nand nand_7 (nand_7_out, nand_6_out, nand_6_out);
  nand nand_8 (nand_8_out, _74ls393_1__2qa, _74ls393_1__2qd);
  Half7474 half7474_18 (.nSD(nand_7_out), .D(1'b1), .CP(1'b1), .nRD(nand_13_out), .Q(TXBusy), .nQ(nTXbusy));
  nand nand_9 (nand_9_out, nand_8_out, nand_8_out);
  Delay #(.delayTime(10)) delay_4 (.in(nResetP), .out(delay_4_out));
  nand nand_10 (nand_10_out, _74ls393_1__1qd, nand_9_out);
  not not_24 (not_24_out, delay_4_out);
  _74LS393 _74ls393_2 (
    ._1A(clk_2), ._1CL(nTXbusy), ._2A(_74ls393_2__1qd), ._2CL(nTXbusy), ._1QD(_74ls393_2__1qd),
    ._2QB(_74ls393_2__2qb), ._2QD(_74ls393_2__2qd));  // open: _1QA, _1QB, _1QC, _2QA, _2QC
  nand nand_11 (nand_11_out, RX, RX);
  Half7474 half7474_19 (.nSD(RX), .D(1'b0), .CP(nReset), .nRD(nand_10_out), .nQ(half7474_19_nq));  // open: Q
  Half7474 half7474_20 (.nSD(nand_10_out), .D(1'b0), .CP(nReset), .nRD(_74ls138_1_ny7), .Q(RX_RDY), .nQ(nRX_RDY));
  and and_30 (and_30_out, nPC_LD, nResetP);
  or or_14 (or_14_out, in_8, not_24_out);
  nand nand_12 (nand_12_out, _74ls393_2__1qd, _74ls393_2__1qd);
  nand nand_13 (nand_13_out, _74ls393_2__2qb, _74ls393_2__2qd);
  _74LS157 _74ls157_1 (
    .S(nResetP), .A1(1'b0), .A2(1'b0), .A3(1'b0), .A4(1'b0), .B1(DBUS[0]), .B2(DBUS[1]), .B3(DBUS[2]),
    .B4(DBUS[3]), .G(1'b0), .Y1(_74ls157_1_y1), .Y2(_74ls157_1_y2), .Y3(_74ls157_1_y3), .Y4(_74ls157_1_y4));
  _74LS157 _74ls157_2 (
    .S(nResetP), .A1(1'b0), .A2(1'b0), .A3(1'b0), .A4(1'b0), .B1(DBUS[4]), .B2(DBUS[5]), .B3(DBUS[6]),
    .B4(DBUS[7]), .G(1'b0), .Y1(_74ls157_2_y1), .Y2(_74ls157_2_y2), .Y3(_74ls157_2_y3), .Y4(_74ls157_2_y4));
  _74LS157 _74ls157_3 (
    .S(nResetP), .A1(1'b0), .A2(1'b0), .A3(1'b0), .A4(1'b0), .B1(DBUS[8]), .B2(DBUS[9]), .B3(DBUS[10]),
    .B4(DBUS[11]), .G(1'b0), .Y1(_74ls157_3_y1), .Y2(_74ls157_3_y2), .Y3(_74ls157_3_y3), .Y4(_74ls157_3_y4));
  _74LS157 _74ls157_4 (
    .S(nResetP), .A1(1'b0), .A2(1'b0), .A3(1'b0), .A4(1'b0), .B1(DBUS[12]), .B2(DBUS[13]), .B3(DBUS[14]),
    .B4(DBUS[15]), .G(1'b0), .Y1(_74ls157_4_y1), .Y2(_74ls157_4_y2), .Y3(_74ls157_4_y3), .Y4(_74ls157_4_y4));
  _74LS157 _74ls157_5 (
    .S(nResetP), .A1(1'b0), .A2(1'b0), .A3(1'b0), .A4(1'b0), .B1(DBUS[16]), .B2(DBUS[17]), .B3(DBUS[18]),
    .B4(DBUS[19]), .G(1'b0), .Y1(_74ls157_5_y1), .Y2(_74ls157_5_y2), .Y3(_74ls157_5_y3), .Y4(_74ls157_5_y4));
  _74LS157 _74ls157_6 (
    .S(nResetP), .A1(1'b0), .A2(PC_FLASH), .A3(PC_FLASH), .A4(1'b0), .B1(DBUS[20]), .B2(DBUS[21]),
    .B3(DBUS[22]), .B4(DBUS[23]), .G(1'b0), .Y1(_74ls157_6_y1), .Y2(_74ls157_6_y2), .Y3(_74ls157_6_y3),
    .Y4(_74ls157_6_y4));
  _74LS165 _74ls165_1 (
    .nLD(half7474_17_nq), .INH(1'b0), .CLK(nand_12_out), .SER(1'b1), .A(1'b1), .B(1'b1), .C(1'b1), .D(1'b1),
    .E(1'b1), .F(1'b1), .G(1'b1), .H(_74ls564_5_nq0[7]), .QH(_74ls165_1_qh));  // open: nQH
  _74LS595 _74ls595_1 (
    .SER(nand_11_out), .SCLK(_74ls393_1__1qd), .RCLK(nand_9_out), .nOE(1'b0), .nCLR(nReset),
    .Q_A(_74ls595_1_q_a[7]), .Q_B(_74ls595_1_q_a[6]), .Q_C(_74ls595_1_q_a[5]), .Q_D(_74ls595_1_q_a[4]),
    .Q_E(_74ls595_1_q_a[3]), .Q_F(_74ls595_1_q_a[2]), .Q_G(_74ls595_1_q_a[1]), .Q_H(_74ls595_1_q_a[0]));  // open: Q_H_2
  and and_31 (and_31_out, _74ls138_1_ny6, _74ls138_1_ny5, pullup_2_out);
  _74LS151 _74ls151_1 (
    .A(_74ls138_1_ny6), .B(_74ls138_1_ny5), .C(pullup_2_out), .S(1'b0), .D0(1'b0), .D1(1'b0), .D2(1'b0),
    .D3(pulldown_39_out), .D4(1'b0), .D5(nTXbusy), .D6(RX_RDY), .D7(1'b0), .Y(_74ls151_1_y));  // open: W
  _74LS541 _74ls541_4 (
    .nOE1(_74ls138_1_ny7), .nOE2(_74ls138_1_ny7), ._0D(_74ls595_1_q_a[7]), ._1D(_74ls595_1_q_a[6]),
    ._2D(_74ls595_1_q_a[5]), ._3D(_74ls595_1_q_a[4]), ._4D(_74ls595_1_q_a[3]), ._5D(_74ls595_1_q_a[2]),
    ._6D(_74ls595_1_q_a[1]), ._7D(_74ls595_1_q_a[0]), ._0O(DBUS[7]), ._1O(DBUS[6]), ._2O(DBUS[5]),
    ._3O(DBUS[4]), ._4O(DBUS[3]), ._5O(DBUS[2]), ._6O(DBUS[1]), ._7O(DBUS[0]));
  // Probe RXCHAR on _74ls595_1_q_a
  _74LS541 _74ls541_5 (
    .nOE1(and_31_out), .nOE2(and_31_out), ._0D(_74ls151_1_y), ._1D(1'b0), ._2D(1'b0), ._3D(1'b0), ._4D(1'b0),
    ._5D(1'b0), ._6D(1'b0), ._7D(1'b0), ._0O(DBUS[0]), ._1O(DBUS[1]), ._2O(DBUS[2]), ._3O(DBUS[3]),
    ._4O(DBUS[4]), ._5O(DBUS[5]), ._6O(DBUS[6]), ._7O(DBUS[7]));
  _74LS163 _74ls163_2 (
    .nPE(and_30_out), .nSR(1'b1), .CP(or_14_out), .CET(1'b1), .CEP(1'b1), .P0(_74ls157_1_y1),
    .P1(_74ls157_1_y2), .P2(_74ls157_1_y3), .P3(_74ls157_1_y4), .TC(_74ls163_2_tc), .Q0(PCbit0),
    .Q1(SPY_PC[1]), .Q2(SPY_PC[2]), .Q3(SPY_PC[3]));
  _74LS163 _74ls163_3 (
    .nPE(and_30_out), .nSR(1'b1), .CP(or_14_out), .CET(_74ls163_2_tc), .CEP(1'b1), .P0(_74ls157_2_y1),
    .P1(_74ls157_2_y2), .P2(_74ls157_2_y3), .P3(_74ls157_2_y4), .TC(_74ls163_3_tc), .Q0(SPY_PC[4]),
    .Q1(SPY_PC[5]), .Q2(SPY_PC[6]), .Q3(SPY_PC[7]));
  _74LS163 _74ls163_4 (
    .nPE(and_30_out), .nSR(1'b1), .CP(or_14_out), .CET(_74ls163_3_tc), .CEP(1'b1), .P0(_74ls157_3_y1),
    .P1(_74ls157_3_y2), .P2(_74ls157_3_y3), .P3(_74ls157_3_y4), .TC(_74ls163_4_tc), .Q0(SPY_PC[8]),
    .Q1(SPY_PC[9]), .Q2(SPY_PC[10]), .Q3(SPY_PC[11]));
  _74LS163 _74ls163_5 (
    .nPE(and_30_out), .nSR(1'b1), .CP(or_14_out), .CET(_74ls163_4_tc), .CEP(1'b1), .P0(_74ls157_4_y1),
    .P1(_74ls157_4_y2), .P2(_74ls157_4_y3), .P3(_74ls157_4_y4), .TC(_74ls163_5_tc), .Q0(SPY_PC[12]),
    .Q1(SPY_PC[13]), .Q2(SPY_PC[14]), .Q3(SPY_PC[15]));
  _74LS163 _74ls163_6 (
    .nPE(and_30_out), .nSR(1'b1), .CP(or_14_out), .CET(_74ls163_5_tc), .CEP(1'b1), .P0(_74ls157_5_y1),
    .P1(_74ls157_5_y2), .P2(_74ls157_5_y3), .P3(_74ls157_5_y4), .TC(_74ls163_6_tc), .Q0(SPY_PC[16]),
    .Q1(SPY_PC[17]), .Q2(SPY_PC[18]), .Q3(SPY_PC[19]));
  _74LS163 _74ls163_7 (
    .nPE(and_30_out), .nSR(1'b1), .CP(or_14_out), .CET(_74ls163_6_tc), .CEP(1'b1), .P0(_74ls157_6_y1),
    .P1(_74ls157_6_y2), .P2(_74ls157_6_y3), .P3(_74ls157_6_y4), .TC(_74ls163_7_tc), .Q0(SPY_PC[20]),
    .Q1(SPY_PC[21]), .Q2(SPY_PC[22]), .Q3(PCneg));
  _74LS165 _74ls165_2 (
    .nLD(half7474_17_nq), .INH(1'b0), .CLK(nand_12_out), .SER(_74ls165_1_qh), .A(_74ls564_5_nq0[6]),
    .B(_74ls564_5_nq0[5]), .C(_74ls564_5_nq0[4]), .D(_74ls564_5_nq0[3]), .E(_74ls564_5_nq0[2]),
    .F(_74ls564_5_nq0[1]), .G(_74ls564_5_nq0[0]), .H(1'b0), .QH(TX));  // open: nQH
  // NotConnected on DBUS[23:8]
  // Probe on TX
  // _74LS245 _74ls245_4: pin names not known; wires that end beside it: 1'b1, nE_PC
  // _74LS245 _74ls245_5: pin names not known; wires that end beside it: 1'b1, nE_PC
  // _74LS245 _74ls245_6: pin names not known; wires that end beside it: 1'b1, nE_PC
  nor nor_12 (nor_12_out, Tick, A, B, C);
  and and_32 (and_32_out, PCneg, not_25_out);
  not not_25 (not_25_out, PCbit0);
  and and_33 (and_33_out, PCneg, PCbit0);
  // Probe PROGRAM COUNTER on {PCneg, SPY_PC, PCbit0}
  // Probe on and_33_out
  Half7474 half7474_21 (.nSD(1'b1), .D(1'b1), .CP(INTREQ), .nRD(half7474_27_nq), .Q(half7474_21_q));  // open: nQ
  Half7474 half7474_22 (.nSD(1'b1), .D(1'b1), .CP(and_32_out), .nRD(half7474_28_nq), .Q(half7474_22_q));  // open: nQ
  Button I (.out(INTREQ));
  LED led_44 (.in(TS0));
  and and_34 (and_34_out, half7474_21_q, nor_12_out);
  and and_35 (and_35_out, nor_12_out, half7474_22_q);
  // Probe on half7474_28_nq
  LED led_45 (.in(TS1));
  LED led_46 (.in(TS2));
  Half7474 half7474_23 (.nSD(1'b1), .D(and_34_out), .CP(Tick), .nRD(half7474_27_nq), .Q(INTA_CK));  // open: nQ
  Half7474 half7474_24 (.nSD(1'b1), .D(and_35_out), .CP(Tick), .nRD(half7474_28_nq), .Q(half7474_24_q));  // open: nQ
  LED led_47 (.in(TS3));
  LED led_48 (.in(TS4));
  Half7474 half7474_25 (.nSD(1'b1), .D(INTA_CK), .CP(Tick), .nRD(half7474_27_nq), .Q(half7474_25_q));  // open: nQ
  Half7474 half7474_26 (.nSD(1'b1), .D(half7474_24_q), .CP(Tick), .nRD(half7474_28_nq), .Q(half7474_26_q));  // open: nQ
  LED led_49 (.in(TS5));
  not not_26 (nINTA_E, and_35_out);
  assign in_10 = and_35_out ? 1'b1 : 1'bz;  // Driver driver_14
  LED led_50 (.in(TS6));
  assign in_10 = and_34_out ? 1'b1 : 1'bz;  // Driver driver_15
  assign in_11 = and_34_out ? 1'b1 : 1'bz;  // Driver driver_16
  assign DBUS = and_34_out ? 24'h6 : 24'bz;  // Driver driver_17
  assign in_8 = half7474_25_q ? 1'b1 : 1'bz;  // Driver driver_18
  Half7474 half7474_27 (
    .nSD(1'b1), .D(half7474_25_q), .CP(Tick), .nRD(half7474_27_nq), .nQ(half7474_27_nq));  // open: Q
  assign in_8 = half7474_26_q ? 1'b1 : 1'bz;  // Driver driver_19
  Half7474 half7474_28 (
    .nSD(1'b1), .D(half7474_26_q), .CP(Tick), .nRD(half7474_28_nq), .nQ(half7474_28_nq));  // open: Q
  LED led_51 (.in(TS7));
  or or_15 (DMA, and_34_out, and_35_out);
  _74LS574 _74ls574_8 (
    .nOC(nINTA_E), .CLK(INTA_CK), .D0(ABUS[0]), .D1(ABUS[1]), .D2(ABUS[2]), .D3(ABUS[3]), .D4(ABUS[4]),
    .D5(ABUS[5]), .D6(ABUS[6]), .D7(ABUS[7]), .Q0(DBUS[0]), .Q1(DBUS[1]), .Q2(DBUS[2]), .Q3(DBUS[3]),
    .Q4(DBUS[4]), .Q5(DBUS[5]), .Q6(DBUS[6]), .Q7(DBUS[7]));
  _74LS574 _74ls574_9 (
    .nOC(nINTA_E), .CLK(INTA_CK), .D0(ABUS[8]), .D1(ABUS[9]), .D2(ABUS[10]), .D3(ABUS[11]), .D4(ABUS[12]),
    .D5(ABUS[13]), .D6(ABUS[14]), .D7(ABUS[15]), .Q0(DBUS[8]), .Q1(DBUS[9]), .Q2(DBUS[10]), .Q3(DBUS[11]),
    .Q4(DBUS[12]), .Q5(DBUS[13]), .Q6(DBUS[14]), .Q7(DBUS[15]));
  _74LS574 _74ls574_10 (
    .nOC(nINTA_E), .CLK(INTA_CK), .D0(ABUS[16]), .D1(ABUS[17]), .D2(ABUS[18]), .D3(ABUS[19]), .D4(ABUS[20]),
    .D5(ABUS[21]), .D6(ABUS[22]), .D7(ABUS[23]), .Q0(DBUS[16]), .Q1(DBUS[17]), .Q2(DBUS[18]), .Q3(DBUS[19]),
    .Q4(DBUS[20]), .Q5(DBUS[21]), .Q6(DBUS[22]), .Q7(DBUS[23]));
  // _74LS574 _74ls574_11: pin names not known; wires that end beside it: 1'b0, INTA_CK
  // _74LS574 _74ls574_12: pin names not known; wires that end beside it: 1'b0, INTA_CK
  // _74LS574 _74ls574_13: pin names not known; wires that end beside it: 1'b0, INTA_CK
  // Probe on DBUS
  // Probe on {undriven_4, undriven_3, undriven_2}

  // Other names for the same wires on the sheet: A_CK = in_6; Aval_CK = in_14; B_CK = in_7; BAUD = clk_2;
  //   Bval_CK = in_15; CK = XTAL; E_PC = in_11; MAR_CK = in_5; MAR_E = in_9; MopEnd = in_17; PC_CK = in_8;
  //   PC_LD = in_10; SPY_PC (some bits) = {PCneg, PCbit0}; RD = in_13; Result_E = in_16; WR = in_12

  // Notes on the sheet:
  //   XTAL: Hz: 2147483647
  //   TraceClock: Hz: 10
  //   GPIO2in: default 80
  //   clk_2: Hz: 153600
  //   RUN/HALT
  //   CONTROL/SEQUENCER
  //   RESET-F
  //   RESET-R
  //   microSTEP
  //   STEP
  //   diode
  //   steering
  //   MAR & NEG
  //   U9
  //   U10
  //   U14
  //   U16
  //   R W 
  //   0 0 = 1
  //   0 1 = 0 
  //   1 0 = 1
  //   1 1 = 1
  //   U20
  //   LATCHED SUBTRACTOR
  //   Carry In
  //   U21
  //   1 x Triple OR (4075)
  //   1 x Quad OR (32)
  //   1 x Quad  NOR (02)
  //   1 x Quad AND (00)
  //   1 x Hex NOT (04)
  //   6 x 7474 FF
  //   1 x 74163 COUNTER
  //   Out Enable
  //   MICROCODE
  //   DECODER
  //   PLAIN
  //   IO
  //   IO-read
  //   IO-write
  //   E_PC
  //   RD
  //   MAR_CK
  //   A_CK
  //   B_CK
  //   MAR_E
  //   Aval_CK
  //   Bval_CK
  //   PC_CK
  //   WR
  //   Res_E
  //   PC_LD
  //   LEQ
  //   A-
  //   B-
  //   if(a < 0) mem[b] += (int)getchar(); /* input */
  //           else if(b < 0) printf("%c", (char)mem[a]); /* output */
  //   stty -icanon -echo && nc localhost 23
  //   GPIO
  //   GPIOw
  //   GPIOr
  //   (-8)
  //   (-7)
  //   (-6)
  //   (-5)
  //   (-4) PORT2Write
  //   (-3)
  //   (-2)
  //   (-1) UARTtxdWrite
  //   (-4) PORT2read
  //   (-3) UARTbusyRead
  //   (-2) UARTavailRead
  //   (-1) UARTrxdRead
  //   INTERRUPT
  //   -----------------------
  //   Save current PC to holding register
  //   Set PC to 6
  //   RETURN FROM INTERRUPT
  //   (initiated by goto -2)
  //   -----------------------
  //   SET PC to holding register
  //   UartTxWr
  //   UARTrxdRead
  //   UARTavailRead
  //   UARTbusyRead
  //   UART
  //   SendCk
  //   ~D
  //   OE
  //   PROGRAM COUNTER
  //   ~Reset
  //   NewPC
  //   Flash
  //   ~OE
  //   ~LD
  //   CK
  //   Neg
  //   INTERUPT
  //   Q
endmodule
