// Digital circuit SUBLEQ24.dig as structural Verilog
module SUBLEQ24 (
  input  XTAL,
  input  TraceClock,
  input  TRACE,
  input  [7:0] GPIO2in,
  input  clk,
  input  clk_2
);

  wire _74ls138_1_ny0, _74ls138_1_ny1, _74ls138_1_ny2, _74ls138_1_ny3, _74ls138_1_ny4, _74ls151_1_y,
       _74ls157_1_y1, _74ls157_1_y2, _74ls157_1_y3, _74ls157_1_y4, _74ls157_2_y1, _74ls157_2_y2,
       _74ls157_2_y3, _74ls157_2_y4, _74ls157_3_y1, _74ls157_3_y2, _74ls157_3_y3, _74ls157_3_y4,
       _74ls157_4_y1, _74ls157_4_y2, _74ls157_4_y3, _74ls157_4_y4, _74ls157_5_y1, _74ls157_5_y2,
       _74ls157_5_y3, _74ls157_5_y4, _74ls157_6_y1, _74ls157_6_y2, _74ls157_6_y3, _74ls157_6_y4,
       _74ls163_1_tc, _74ls163_2_tc, _74ls163_3_tc, _74ls163_4_tc, _74ls163_5_tc, _74ls163_6_tc,
       _74ls165_1_qh, _74ls175_1_q1, _74ls175_1_q2, _74ls175_1_q3, _74ls175_1_q4, _74ls175_2_nq1,
       _74ls175_2_nq2, _74ls175_2_nq3, _74ls175_2_nq4, _74ls175_3_p3, _74ls175_3_p4, _74ls175_3_p5,
       _74ls175_3_p6, _74ls175_4_p3, _74ls175_4_p4, _74ls175_4_p5, _74ls175_4_p6, _74ls238_1_y0,
       _74ls238_1_y1, _74ls238_1_y2, _74ls238_1_y3, _74ls238_1_y4, _74ls238_1_y5, _74ls238_1_y6,
       _74ls238_1_y7, _74ls238_2_y0, _74ls238_2_y1, _74ls238_2_y2, _74ls238_2_y3, _74ls238_2_y4,
       _74ls238_2_y5, _74ls238_2_y6, _74ls283_1_p2, _74ls283_2_p2, _74ls283_3_p2, _74ls283_4_p2,
       _74ls283_5_p2, _74ls393_1__1qd, _74ls393_1__2qa, _74ls393_1__2qd, _74ls393_2__1qd, _74ls393_2__2qb,
       _74ls393_2__2qd, _74ls540_1_n6o, _74ls540_1_n7o, _74ls541_4__7o, A_CK, AisNeg, and_1_out, and_2_out,
       and_3_out, and_4_out, and_5_out, and_6_out, and_7_out, and_8_out, and_9_out, and_10_out, and_11_out,
       and_12_out, and_13_out, and_14_out, and_15_out, Aval_CK, B_CK, BisNeg, Bval_CK, d_ff_1_q, d_ff_2_q,
       delay_1_out, delay_2_out, half7474_3_nq, half7474_3_q, half7474_4_q, half7474_5_q, half7474_6_nq,
       half7474_9_nq, half7474_11_nq, half7474_13_q, half7474_14_nq, half7474_14_q, half7474_15_q,
       half7474_16_nq, half7474_16_q, half7474_17_q, half7474_18_q, half7474_19_nq, half7474_20_q, INTREQ,
       IOread, IOwrite, isLEQ, M0, M1, M2, M_out, MAR_CK, MopEnd, nand_1_out, nand_2_out, nand_4_out,
       nand_5_out, nand_6_out, nand_8_out, nand_9_out, nand_10_out, nand_11_out, nand_12_out, nand_13_out,
       nand_14_out, nand_15_out, nBusRq, nCK, nE_PC, nIOread, nIOreadP, nIOwrite, nIOwriteP, nMAR_E,
       nor_2_out, nor_3_out, nor_4_out, nor_5_out, nor_6_out, nor_7_out, nor_8_out, nor_9_out, nor_10_out,
       not_1_out, not_3_out, not_7_out, not_8_out, not_9_out, not_10_out, not_11_out, not_13_out, not_14_out,
       not_15_out, not_16_out, not_17_out, not_18_out, not_19_out, nPC_LD, nRD, nResetP, nResetX, nResult_E,
       nRX_RDY, nTXbusy, nUARTavailRead, nUARTbusyRead, nUARTrxdRead, nWR, or_1_out, or_2_out, or_3_out,
       or_4_out, or_5_out, or_6_out, or_8_out, or_9_out, or_10_out, or_11_out, or_12_out, or_13_out,
       or_14_out, or_15_out, or_16_out, PC_CK, PC_FLASH, PC_LD, PCbit0, PCneg, POR, pulldown_10_out,
       pullup_8_out, R_out, RUN, RX, RX_RDY, S_out, Tick, TS0, TS1, TS2, TS3, TS4, TS5, TS6, TS7, TX, TXBusy,
       UARTtxdWrite, Z_out;
  wire [7:0] _74ls564_5_nq7, _74ls595_1_q_f, PORT2OUT;
  wire [19:0] barrelshifter_1_out, counter_1_out, d_ff_4_q;
  wire [22:1] SPY_PC;
  wire [23:0] ABUS, d_ff_5_q, DBUS, not_5_out, not_6_out, ramasync_1_q, SPY_aval, SPY_bval, SPY_sub;

  Button R (.out(R_out));
  Button S (.out(S_out));
  and and_1 (and_1_out, PCneg, PCbit0);
  and and_2 (and_2_out, TRACE, TraceClock);
  not not_1 (not_1_out, TS0);
  Button F (.out(PC_FLASH));
  Button Z (.out(Z_out));
  // Probe on and_1_out
  or or_1 (or_1_out, R_out, S_out, and_2_out);
  // Probe on ABUS
  or or_2 (or_2_out, nWR, POR);
  and and_3 (and_3_out, not_1_out, nResetX);
  or or_3 (or_3_out, PC_FLASH, Z_out, Z_out);
  or or_4 (or_4_out, ~or_2_out, nRD);  // Or
  LED led_1 (.in(or_3_out));
  RAMAsync #(.AddrBits(24), .isProgramMemory("true"), .Bits(24)) ramasync_1 (
    .A(ABUS), .D(DBUS), .we(~or_2_out), .Q(ramasync_1_q));
  // _74LS574 _74ls574_1: pin names not known; wires that end beside it: nMAR_E, MAR_CK
  // _74LS574 _74ls574_2: pin names not known; wires that end beside it: nMAR_E, MAR_CK
  // _74LS574 _74ls574_3: pin names not known; wires that end beside it: nMAR_E, MAR_CK
  Half7474 half7474_1 (.nSD(1'b1), .D(DBUS[23]), .CP(A_CK), .nRD(and_3_out), .Q(AisNeg));  // open: nQ
  Half7474 half7474_2 (.nSD(1'b1), .D(DBUS[23]), .CP(B_CK), .nRD(and_3_out), .Q(BisNeg));  // open: nQ
  not not_2 (nResetX, or_3_out);
  _74LS175 _74ls175_1 (
    .D1(or_3_out), .D2(and_1_out), .D3(R_out), .D4(or_1_out), .CLK(XTAL), .nCL(nResetP), .Q1(_74ls175_1_q1),
    .Q2(_74ls175_1_q2), .Q3(_74ls175_1_q3), .Q4(_74ls175_1_q4));  // open: nQ1, nQ2, nQ3, nQ4
  assign DBUS = ~or_4_out ? ramasync_1_q : 24'bz;  // DriverInvSel driverinvsel_1
  PullDown #(.Bits(24)) pulldown_1 (.out(DBUS));
  // Probe on DBUS
  _74LS175 _74ls175_2 (
    .D1(_74ls175_1_q1), .D2(_74ls175_1_q2), .D3(_74ls175_1_q3), .D4(_74ls175_1_q4), .CLK(XTAL),
    .nCL(nResetP), .nQ1(_74ls175_2_nq1), .nQ2(_74ls175_2_nq2), .nQ3(_74ls175_2_nq3), .nQ4(_74ls175_2_nq4));  // open: Q1, Q2, Q3, Q4
  D_FF d_ff_1 (.D(1'b1), .C(TraceClock), .Q(d_ff_1_q));  // open: nQ
  D_FF d_ff_2 (.D(d_ff_1_q), .C(TraceClock), .Q(d_ff_2_q));  // open: nQ
  and and_4 (and_4_out, _74ls175_1_q1, _74ls175_2_nq1);
  and and_5 (and_5_out, _74ls175_1_q2, _74ls175_2_nq2);
  and and_6 (and_6_out, _74ls175_1_q3, _74ls175_2_nq3);
  and and_7 (and_7_out, _74ls175_1_q4, _74ls175_2_nq4);
  D_FF d_ff_3 (.D(d_ff_2_q), .C(TraceClock), .nQ(POR));  // open: Q
  or or_5 (or_5_out, and_5_out, and_6_out);
  not not_3 (not_3_out, and_7_out);
  // _74LS564 _74ls564_1: pin names not known; wires that end beside it: 1'b0, Aval_CK
  // _74LS564 _74ls564_2: pin names not known; wires that end beside it: 1'b0, Aval_CK
  // _74LS564 _74ls564_3: pin names not known; wires that end beside it: 1'b0, Aval_CK
  // _74LS574 _74ls574_4: pin names not known; wires that end beside it: 1'b0, Bval_CK
  // _74LS574 _74ls574_5: pin names not known; wires that end beside it: 1'b0, Bval_CK
  // _74LS574 _74ls574_6: pin names not known; wires that end beside it: 1'b0, Bval_CK
  nor nor_1 (nResetP, POR, and_4_out);
  Half7474 half7474_3 (
    .nSD(1'b1), .D(half7474_3_nq), .CP(or_5_out), .nRD(nResetP), .Q(half7474_3_q), .nQ(half7474_3_nq));
  // Probe on not_3_out
  Half7474 half7474_4 (.nSD(not_3_out), .D(1'b0), .CP(MopEnd), .nRD(nResetP), .Q(half7474_4_q));  // open: nQ
  // Probe on nResetP
  LED led_2 (.in(half7474_4_q));
  not not_4 (nCK, XTAL);
  LED led_3 (.in(nResetP));
  Button M (.out(M_out));
  LED led_4 (.in(half7474_3_q));
  // Probe on half7474_3_q
  or or_6 (or_6_out, half7474_3_q, half7474_4_q);
  // Probe on half7474_4_q
  PullDown pulldown_2 (.out(half7474_4_q));
  Counter #(.Bits(20)) counter_1 (.en(1'b1), .C(TS0), .clr(clk), .out(counter_1_out));  // open: ovf
  Half7474 half7474_5 (.nSD(1'b1), .D(M_out), .CP(nCK), .nRD(nResetP), .Q(half7474_5_q));  // open: nQ
  Half7474 half7474_6 (.nSD(1'b1), .D(or_6_out), .CP(nCK), .nRD(nResetP), .Q(RUN), .nQ(half7474_6_nq));
  // _74LS283 _74ls283_1: pin names not known; wires that end beside it: nIOwrite, _74ls283_1_p2
  // _74LS283 _74ls283_2: pin names not known; wires that end beside it: _74ls283_1_p2, _74ls283_2_p2
  // _74LS283 _74ls283_3: pin names not known; wires that end beside it: _74ls283_2_p2, _74ls283_3_p2
  // _74LS283 _74ls283_4: pin names not known; wires that end beside it: _74ls283_3_p2, _74ls283_4_p2
  // _74LS283 _74ls283_5: pin names not known; wires that end beside it: _74ls283_4_p2, _74ls283_5_p2
  // _74LS283 _74ls283_6: pin names not known; wires that end beside it: _74ls283_5_p2
  LED u_RUN (.in(RUN));
  // Probe on half7474_6_nq
  D_FF #(.Bits(20)) d_ff_4 (.D(counter_1_out), .C(clk), .Q(d_ff_4_q));  // open: nQ
  nor nor_2 (nor_2_out, half7474_6_nq, nCK);
  BarrelShifter #(.Bits(20)) barrelshifter_1 (.in(d_ff_4_q), .shift(5'b00011), .out(barrelshifter_1_out));
  // Probe on barrelshifter_1_out
  or or_7 (Tick, and_4_out, half7474_5_q, nor_2_out);
  D_FF #(.Bits(24)) d_ff_5 (.D(DBUS), .C(MAR_CK), .Q(d_ff_5_q));  // open: nQ
  assign not_5_out = ~SPY_sub;  // Not not_5, 24 bits wide
  assign not_6_out = ~SPY_aval;  // Not not_6, 24 bits wide
  PullUp #(.Bits(24)) pullup_1 (.out(SPY_aval));
  PullDown #(.Bits(24)) pulldown_3 (.out(SPY_bval));
  _74LS245 _74ls245_1 (
    .DIR(1'b1), .A1(SPY_sub[0]), .A2(SPY_sub[1]), .A3(SPY_sub[2]), .A4(SPY_sub[3]), .A5(SPY_sub[4]),
    .A6(SPY_sub[5]), .A7(SPY_sub[6]), .A8(SPY_sub[7]), .nOE(nResult_E), .B1(DBUS[0]), .B2(DBUS[1]),
    .B3(DBUS[2]), .B4(DBUS[3]), .B5(DBUS[4]), .B6(DBUS[5]), .B7(DBUS[6]), .B8(DBUS[7]));
  _74LS245 _74ls245_2 (
    .DIR(1'b1), .A1(SPY_sub[8]), .A2(SPY_sub[9]), .A3(SPY_sub[10]), .A4(SPY_sub[11]), .A5(SPY_sub[12]),
    .A6(SPY_sub[13]), .A7(SPY_sub[14]), .A8(SPY_sub[15]), .nOE(nResult_E), .B1(DBUS[8]), .B2(DBUS[9]),
    .B3(DBUS[10]), .B4(DBUS[11]), .B5(DBUS[12]), .B6(DBUS[13]), .B7(DBUS[14]), .B8(DBUS[15]));
  _74LS245 _74ls245_3 (
    .DIR(1'b1), .A1(SPY_sub[16]), .A2(SPY_sub[17]), .A3(SPY_sub[18]), .A4(SPY_sub[19]), .A5(SPY_sub[20]),
    .A6(SPY_sub[21]), .A7(SPY_sub[22]), .A8(SPY_sub[23]), .nOE(nResult_E), .B1(DBUS[16]), .B2(DBUS[17]),
    .B3(DBUS[18]), .B4(DBUS[19]), .B5(DBUS[20]), .B6(DBUS[21]), .B7(DBUS[22]), .B8(DBUS[23]));
  not not_7 (not_7_out, MopEnd);
  _74LS161 _74ls161_1 (
    .nLD(not_7_out), .nCLR(nResetP), .CLK(Tick), .ENT(1'b1), .ENP(nBusRq), .A(1'b0), .B(1'b0), .C(1'b0),
    .D(1'b0), .QA(M0), .QB(M1), .QC(M2));  // open: RCO, QD
  // Probe on Tick
  // Probe MAR on d_ff_5_q
  // Probe PC on {PCneg, SPY_PC, PCbit0}
  // Probe SUBT on SPY_sub
  // Probe ~SUBT on not_5_out
  // Probe ~AVAL on not_6_out
  // Probe BVAL on SPY_bval
  nor nor_3 (nor_3_out, SPY_sub[3], SPY_sub[2], SPY_sub[1]);
  nor nor_4 (nor_4_out, SPY_sub[0], SPY_sub[7], SPY_sub[6]);
  nor nor_5 (nor_5_out, SPY_sub[5], SPY_sub[4], SPY_sub[11]);
  nor nor_6 (nor_6_out, SPY_sub[10], SPY_sub[9], SPY_sub[8]);
  nor nor_7 (nor_7_out, SPY_sub[15], SPY_sub[14], SPY_sub[13]);
  nor nor_8 (nor_8_out, SPY_sub[12], SPY_sub[19], SPY_sub[18]);
  nor nor_9 (nor_9_out, SPY_sub[17], SPY_sub[16], SPY_sub[23]);
  nor nor_10 (nor_10_out, SPY_sub[22], SPY_sub[21], SPY_sub[20]);
  nand nand_1 (nand_1_out, nor_3_out, nor_4_out, nor_5_out, nor_6_out, nor_7_out, nor_8_out, nor_9_out, nor_10_out);
  nand nand_2 (nand_2_out, SPY_sub[23], SPY_sub[23]);
  nand nand_3 (isLEQ, nand_2_out, nand_1_out);
  Delay #(.delayTime(5)) delay_1 (.in(not_8_out), .out(delay_1_out));
  not not_8 (not_8_out, Tick);
  _74LS238 _74ls238_1 (
    .A(M0), .B(M1), .C(M2), .G(1'b1), .nGA(1'b0), .nGB(1'b0), .Y0(_74ls238_1_y0), .Y1(_74ls238_1_y1),
    .Y2(_74ls238_1_y2), .Y3(_74ls238_1_y3), .Y4(_74ls238_1_y4), .Y5(_74ls238_1_y5), .Y6(_74ls238_1_y6),
    .Y7(_74ls238_1_y7));
  LED led_5 (.in(TS0));
  not not_9 (not_9_out, delay_1_out);
  not not_10 (not_10_out, TS0);
  nand nand_4 (nand_4_out, TS3, BisNeg);
  nand nand_5 (nand_5_out, TS1, AisNeg);
  LED led_6 (.in(TS1));
  _74LS574 _74ls574_7 (
    .nOC(1'b0), .CLK(not_9_out), .D0(_74ls238_1_y0), .D1(_74ls238_1_y1), .D2(_74ls238_1_y2),
    .D3(_74ls238_1_y3), .D4(_74ls238_1_y4), .D5(_74ls238_1_y5), .D6(_74ls238_1_y6), .D7(_74ls238_1_y7),
    .Q0(TS0), .Q1(TS1), .Q2(TS2), .Q3(TS3), .Q4(TS4), .Q5(TS5), .Q6(TS6), .Q7(TS7));  // open: SPY
  LED led_7 (.in(TS2));
  // _74LS175 _74ls175_3: pin names not known; wires that end beside it: B_CK, 1'b1, _74ls175_3_p3, _74ls175_3_p4, _74ls175_3_p5, _74ls175_3_p6
  // Probe on nIOwriteP
  // _74LS175 _74ls175_4: pin names not known; wires that end beside it: A_CK, 1'b1, _74ls175_4_p3, _74ls175_4_p4, _74ls175_4_p5, _74ls175_4_p6
  // Probe on nIOreadP
  Half7474 half7474_7 (.nSD(nand_4_out), .D(1'b0), .CP(nResetP), .nRD(not_10_out), .Q(IOwrite), .nQ(nIOwrite));
  Half7474 half7474_8 (.nSD(nand_5_out), .D(1'b0), .CP(nResetP), .nRD(not_10_out), .Q(IOread), .nQ(nIOread));
  LED led_8 (.in(TS3));
  LED led_9 (.in(TS4));
  // Probe on IOwrite
  // Probe on IOread
  LED led_10 (.in(TS5));
  _74LS238 _74ls238_2 (
    .A(_74ls175_3_p3), .B(_74ls175_3_p4), .C(_74ls175_3_p5), .G(1'b1), .nGA(_74ls175_3_p6), .nGB(nIOwriteP),
    .Y0(_74ls238_2_y0), .Y1(_74ls238_2_y1), .Y2(_74ls238_2_y2), .Y3(_74ls238_2_y3), .Y4(_74ls238_2_y4),
    .Y5(_74ls238_2_y5), .Y6(_74ls238_2_y6), .Y7(UARTtxdWrite));
  _74LS138 _74ls138_1 (
    .A(_74ls175_4_p3), .B(_74ls175_4_p4), .C(_74ls175_4_p5), .G(1'b1), .nGB(_74ls175_4_p6), .nGA(nIOreadP),
    .nY0(_74ls138_1_ny0), .nY1(_74ls138_1_ny1), .nY2(_74ls138_1_ny2), .nY3(_74ls138_1_ny3),
    .nY4(_74ls138_1_ny4), .nY5(nUARTbusyRead), .nY6(nUARTavailRead), .nY7(nUARTrxdRead));
  LED led_11 (.in(TS6));
  nand nand_6 (nand_6_out, TS4, IOwrite);
  nand nand_7 (nIOreadP, TS3, IOread);
  _74LS541 _74ls541_1 (
    .nOE1(_74ls138_1_ny4), .nOE2(_74ls138_1_ny4), ._0D(GPIO2in[0]), ._1D(GPIO2in[1]), ._2D(GPIO2in[2]),
    ._3D(GPIO2in[3]), ._4D(GPIO2in[4]), ._5D(GPIO2in[5]), ._6D(GPIO2in[6]), ._7D(GPIO2in[7]), ._0O(DBUS[0]),
    ._1O(DBUS[1]), ._2O(DBUS[2]), ._3O(DBUS[3]), ._4O(DBUS[4]), ._5O(DBUS[5]), ._6O(DBUS[6]), ._7O(DBUS[7]));
  _74LS541 _74ls541_2 (
    .nOE1(nIOreadP), .nOE2(nIOreadP), ._0D(1'b0), ._1D(1'b0), ._2D(1'b0), ._3D(1'b0), ._4D(1'b0), ._5D(1'b0),
    ._6D(1'b0), ._7D(1'b0), ._0O(DBUS[8]), ._1O(DBUS[9]), ._2O(DBUS[10]), ._3O(DBUS[11]), ._4O(DBUS[12]),
    ._5O(DBUS[13]), ._6O(DBUS[14]), ._7O(DBUS[15]));
  _74LS541 _74ls541_3 (
    .nOE1(nIOreadP), .nOE2(nIOreadP), ._0D(1'b0), ._1D(1'b0), ._2D(1'b0), ._3D(1'b0), ._4D(1'b0), ._5D(1'b0),
    ._6D(1'b0), ._7D(1'b0), ._0O(DBUS[16]), ._1O(DBUS[17]), ._2O(DBUS[18]), ._3O(DBUS[19]), ._4O(DBUS[20]),
    ._5O(DBUS[21]), ._6O(DBUS[22]), ._7O(DBUS[23]));
  not not_11 (not_11_out, nand_6_out);
  not not_12 (nIOwriteP, not_11_out);
  // Probe on _74ls238_2_y0
  // Probe on _74ls238_2_y1
  // Probe on _74ls238_2_y2
  // Probe on _74ls238_2_y3
  // Probe on _74ls238_2_y4
  // Probe on _74ls238_2_y5
  // Probe on _74ls238_2_y6
  // Probe on UARTtxdWrite
  and and_8 (and_8_out, TS3, nIOread, 1'b1);
  // _74LS564 _74ls564_4: pin names not known; wires that end beside it: 1'b0, _74ls238_2_y4
  // Probe on _74ls138_1_ny0
  // Probe on _74ls138_1_ny1
  // Probe on _74ls138_1_ny2
  // Probe on _74ls138_1_ny3
  // Probe on _74ls138_1_ny4
  // Probe on nUARTbusyRead
  // Probe on nUARTavailRead
  // Probe on nUARTrxdRead
  not not_13 (not_13_out, nBusRq);
  or or_8 (or_8_out, TS0, TS1, TS2);
  // Probe on PORT2OUT
  or or_9 (or_9_out, TS1, TS3, TS6);
  or or_10 (or_10_out, TS1, TS3, 1'b0);
  or or_11 (or_11_out, TS1, TS3, TS4);
  and and_9 (and_9_out, TS4, nIOwrite, 1'b1);
  and and_10 (and_10_out, TS5, nIOwrite, isLEQ);
  or or_12 (or_12_out, TS0, TS2, TS5);
  or or_13 (or_13_out, or_8_out, TS5, and_8_out);
  _74LS541 _74ls541_4 (
    .nOE1(not_13_out), .nOE2(not_13_out), ._0D(TS1), ._1D(TS3), ._2D(TS2), ._3D(TS4), ._4D(TS6),
    ._5D(or_9_out), ._6D(or_10_out), ._7D(1'b0), ._0O(A_CK), ._1O(B_CK), ._2O(Aval_CK), ._3O(Bval_CK),
    ._4O(MopEnd), ._5O(PC_CK), ._6O(MAR_CK), ._7O(_74ls541_4__7o));
  _74LS540 _74ls540_1 (
    .nOE1(not_13_out), .nOE2(not_13_out), ._0D(TS4), ._1D(or_11_out), ._2D(and_9_out), ._3D(and_10_out),
    ._4D(or_12_out), ._5D(or_13_out), ._6D(1'b0), ._7D(1'b0), .n0O(nResult_E), .n1O(nMAR_E), .n2O(nWR),
    .n3O(nPC_LD), .n4O(nE_PC), .n5O(nRD), .n6O(_74ls540_1_n6o), .n7O(_74ls540_1_n7o));
  PullDown pulldown_4 (.out(A_CK));
  PullDown pulldown_5 (.out(B_CK));
  PullUp pullup_2 (.out(nResult_E));
  PullUp pullup_3 (.out(nMAR_E));
  PullDown pulldown_6 (.out(Aval_CK));
  PullDown pulldown_7 (.out(Bval_CK));
  PullDown pulldown_8 (.out(MopEnd));
  PullDown pulldown_9 (.out(PC_CK));
  PullUp pullup_4 (.out(nWR));
  PullUp pullup_5 (.out(nPC_LD));
  PullUp pullup_6 (.out(nE_PC));
  PullUp pullup_7 (.out(nRD));
  PullUp pullup_8 (.out(pullup_8_out));
  PullDown pulldown_10 (.out(pulldown_10_out));
  PullDown pulldown_11 (.out(MAR_CK));
  PullDown pulldown_12 (.out(_74ls541_4__7o));
  PullUp pullup_9 (.out(_74ls540_1_n6o));
  PullUp pullup_10 (.out(_74ls540_1_n7o));
  Half7474 half7474_9 (.nSD(1'b1), .D(1'b1), .CP(UARTtxdWrite), .nRD(nTXbusy), .nQ(half7474_9_nq));  // open: Q
  _74LS564 _74ls564_5 (
    .nOC(1'b0), .CLK(UARTtxdWrite), .D0(DBUS[0]), .D1(DBUS[1]), .D2(DBUS[2]), .D3(DBUS[3]), .D4(DBUS[4]),
    .D5(DBUS[5]), .D6(DBUS[6]), .D7(DBUS[7]), .nQ0(_74ls564_5_nq7[0]), .nQ1(_74ls564_5_nq7[1]),
    .nQ2(_74ls564_5_nq7[2]), .nQ3(_74ls564_5_nq7[3]), .nQ4(_74ls564_5_nq7[4]), .nQ5(_74ls564_5_nq7[5]),
    .nQ6(_74ls564_5_nq7[6]), .nQ7(_74ls564_5_nq7[7]));
  nand nand_8 (nand_8_out, half7474_9_nq, nResetX);
  _74LS393 _74ls393_1 (
    ._1A(clk_2), ._1CL(half7474_11_nq), ._2A(_74ls393_1__1qd), ._2CL(half7474_11_nq), ._1QD(_74ls393_1__1qd),
    ._2QA(_74ls393_1__2qa), ._2QD(_74ls393_1__2qd));  // open: _1QA, _1QB, _1QC, _2QB, _2QC
  // Probe TXCHAR on _74ls564_5_nq7
  nand nand_9 (nand_9_out, _74ls393_1__2qa, _74ls393_1__2qd);
  nand nand_10 (nand_10_out, nand_8_out, nand_8_out);
  Half7474 half7474_10 (.nSD(nand_10_out), .D(1'b1), .CP(1'b1), .nRD(nand_15_out), .Q(TXBusy), .nQ(nTXbusy));
  nand nand_11 (nand_11_out, nand_9_out, nand_9_out);
  nand nand_12 (nand_12_out, _74ls393_1__1qd, nand_11_out);
  Uart_Telnet_GW uart_telnet_gw_1 (.RX(TX), .CLK(clk_2), .TX(RX));
  _74LS393 _74ls393_2 (
    ._1A(clk_2), ._1CL(nTXbusy), ._2A(_74ls393_2__1qd), ._2CL(nTXbusy), ._1QD(_74ls393_2__1qd),
    ._2QB(_74ls393_2__2qb), ._2QD(_74ls393_2__2qd));  // open: _1QA, _1QB, _1QC, _2QA, _2QC
  nand nand_13 (nand_13_out, RX, RX);
  Half7474 half7474_11 (.nSD(RX), .D(1'b0), .CP(nResetX), .nRD(nand_12_out), .nQ(half7474_11_nq));  // open: Q
  Half7474 half7474_12 (.nSD(nand_12_out), .D(1'b0), .CP(nResetX), .nRD(nUARTrxdRead), .Q(RX_RDY), .nQ(nRX_RDY));
  nand nand_14 (nand_14_out, _74ls393_2__1qd, _74ls393_2__1qd);
  nand nand_15 (nand_15_out, _74ls393_2__2qb, _74ls393_2__2qd);
  _74LS595 _74ls595_1 (
    .SER(nand_13_out), .SCLK(_74ls393_1__1qd), .RCLK(nand_11_out), .nOE(1'b0), .nCLR(nResetX),
    .Q_A(_74ls595_1_q_f[7]), .Q_B(_74ls595_1_q_f[6]), .Q_C(_74ls595_1_q_f[5]), .Q_D(_74ls595_1_q_f[4]),
    .Q_E(_74ls595_1_q_f[3]), .Q_F(_74ls595_1_q_f[2]), .Q_G(_74ls595_1_q_f[1]), .Q_H(_74ls595_1_q_f[0]));  // open: Q_H_2
  _74LS165 _74ls165_1 (
    .nLD(half7474_9_nq), .INH(1'b0), .CLK(nand_14_out), .SER(1'b1), .A(1'b1), .B(1'b1), .C(1'b1), .D(1'b1),
    .E(1'b1), .F(1'b1), .G(1'b1), .H(_74ls564_5_nq7[7]), .QH(_74ls165_1_qh));  // open: nQH
  and and_11 (and_11_out, nUARTavailRead, nUARTbusyRead, pullup_8_out);
  _74LS151 _74ls151_1 (
    .A(nUARTavailRead), .B(nUARTbusyRead), .C(pullup_8_out), .S(1'b0), .D0(1'b0), .D1(1'b0), .D2(1'b0),
    .D3(pulldown_10_out), .D4(1'b0), .D5(nTXbusy), .D6(RX_RDY), .D7(1'b0), .Y(_74ls151_1_y));  // open: W
  _74LS541 _74ls541_5 (
    .nOE1(nUARTrxdRead), .nOE2(nUARTrxdRead), ._0D(_74ls595_1_q_f[7]), ._1D(_74ls595_1_q_f[6]),
    ._2D(_74ls595_1_q_f[5]), ._3D(_74ls595_1_q_f[4]), ._4D(_74ls595_1_q_f[3]), ._5D(_74ls595_1_q_f[2]),
    ._6D(_74ls595_1_q_f[1]), ._7D(_74ls595_1_q_f[0]), ._0O(DBUS[7]), ._1O(DBUS[6]), ._2O(DBUS[5]),
    ._3O(DBUS[4]), ._4O(DBUS[3]), ._5O(DBUS[2]), ._6O(DBUS[1]), ._7O(DBUS[0]));
  // Probe RXCHAR on _74ls595_1_q_f
  _74LS541 _74ls541_6 (
    .nOE1(and_11_out), .nOE2(and_11_out), ._0D(_74ls151_1_y), ._1D(1'b0), ._2D(1'b0), ._3D(1'b0), ._4D(1'b0),
    ._5D(1'b0), ._6D(1'b0), ._7D(1'b0), ._0O(DBUS[0]), ._1O(DBUS[1]), ._2O(DBUS[2]), ._3O(DBUS[3]),
    ._4O(DBUS[4]), ._5O(DBUS[5]), ._6O(DBUS[6]), ._7O(DBUS[7]));
  _74LS165 _74ls165_2 (
    .nLD(half7474_9_nq), .INH(1'b0), .CLK(nand_14_out), .SER(_74ls165_1_qh), .A(_74ls564_5_nq7[6]),
    .B(_74ls564_5_nq7[5]), .C(_74ls564_5_nq7[4]), .D(_74ls564_5_nq7[3]), .E(_74ls564_5_nq7[2]),
    .F(_74ls564_5_nq7[1]), .G(_74ls564_5_nq7[0]), .H(1'b0), .QH(TX));  // open: nQH
  // NotConnected on DBUS[23:8]
  not not_14 (not_14_out, delay_2_out);
  Delay #(.delayTime(10)) delay_2 (.in(nResetP), .out(delay_2_out));
  and and_12 (and_12_out, nPC_LD, nResetP);
  or or_14 (or_14_out, PC_CK, not_14_out);
  _74LS157 _74ls157_1 (
    .S(nResetP), .A1(1'b0), .A2(1'b0), .A3(1'b0), .A4(1'b0), .B1(DBUS[0]), .B2(DBUS[1]), .B3(DBUS[2]),
    .B4(DBUS[3]), .G(1'b0), .Y1(_74ls157_1_y1), .Y2(_74ls157_1_y2), .Y3(_74ls157_1_y3), .Y4(_74ls157_1_y4));
  _74LS157 _74ls157_2 (
    .S(nResetP), .A1(1'b0), .A2(1'b0), .A3(1'b0), .A4(1'b0), .B1(DBUS[4]), .B2(DBUS[5]), .B3(DBUS[6]),
    .B4(DBUS[7]), .G(1'b0), .Y1(_74ls157_2_y1), .Y2(_74ls157_2_y2), .Y3(_74ls157_2_y3), .Y4(_74ls157_2_y4));
  _74LS157 _74ls157_3 (
    .S(nResetP), .A1(1'b0), .A2(1'b0), .A3(1'b0), .A4(1'b0), .B1(DBUS[8]), .B2(DBUS[9]), .B3(DBUS[10]),
    .B4(DBUS[11]), .G(1'b0), .Y1(_74ls157_3_y1), .Y2(_74ls157_3_y2), .Y3(_74ls157_3_y3), .Y4(_74ls157_3_y4));
  _74LS157 _74ls157_4 (
    .S(nResetP), .A1(1'b0), .A2(1'b0), .A3(1'b0), .A4(1'b0), .B1(DBUS[12]), .B2(DBUS[13]), .B3(DBUS[14]),
    .B4(DBUS[15]), .G(1'b0), .Y1(_74ls157_4_y1), .Y2(_74ls157_4_y2), .Y3(_74ls157_4_y3), .Y4(_74ls157_4_y4));
  _74LS157 _74ls157_5 (
    .S(nResetP), .A1(1'b0), .A2(1'b0), .A3(1'b0), .A4(1'b0), .B1(DBUS[16]), .B2(DBUS[17]), .B3(DBUS[18]),
    .B4(DBUS[19]), .G(1'b0), .Y1(_74ls157_5_y1), .Y2(_74ls157_5_y2), .Y3(_74ls157_5_y3), .Y4(_74ls157_5_y4));
  _74LS157 _74ls157_6 (
    .S(nResetP), .A1(1'b0), .A2(PC_FLASH), .A3(PC_FLASH), .A4(1'b0), .B1(DBUS[20]), .B2(DBUS[21]),
    .B3(DBUS[22]), .B4(DBUS[23]), .G(1'b0), .Y1(_74ls157_6_y1), .Y2(_74ls157_6_y2), .Y3(_74ls157_6_y3),
    .Y4(_74ls157_6_y4));
  _74LS163 _74ls163_1 (
    .nPE(and_12_out), .nSR(1'b1), .CP(or_14_out), .CET(1'b1), .CEP(1'b1), .P0(_74ls157_1_y1),
    .P1(_74ls157_1_y2), .P2(_74ls157_1_y3), .P3(_74ls157_1_y4), .TC(_74ls163_1_tc), .Q0(PCbit0),
    .Q1(SPY_PC[1]), .Q2(SPY_PC[2]), .Q3(SPY_PC[3]));
  _74LS163 _74ls163_2 (
    .nPE(and_12_out), .nSR(1'b1), .CP(or_14_out), .CET(_74ls163_1_tc), .CEP(1'b1), .P0(_74ls157_2_y1),
    .P1(_74ls157_2_y2), .P2(_74ls157_2_y3), .P3(_74ls157_2_y4), .TC(_74ls163_2_tc), .Q0(SPY_PC[4]),
    .Q1(SPY_PC[5]), .Q2(SPY_PC[6]), .Q3(SPY_PC[7]));
  _74LS163 _74ls163_3 (
    .nPE(and_12_out), .nSR(1'b1), .CP(or_14_out), .CET(_74ls163_2_tc), .CEP(1'b1), .P0(_74ls157_3_y1),
    .P1(_74ls157_3_y2), .P2(_74ls157_3_y3), .P3(_74ls157_3_y4), .TC(_74ls163_3_tc), .Q0(SPY_PC[8]),
    .Q1(SPY_PC[9]), .Q2(SPY_PC[10]), .Q3(SPY_PC[11]));
  _74LS163 _74ls163_4 (
    .nPE(and_12_out), .nSR(1'b1), .CP(or_14_out), .CET(_74ls163_3_tc), .CEP(1'b1), .P0(_74ls157_4_y1),
    .P1(_74ls157_4_y2), .P2(_74ls157_4_y3), .P3(_74ls157_4_y4), .TC(_74ls163_4_tc), .Q0(SPY_PC[12]),
    .Q1(SPY_PC[13]), .Q2(SPY_PC[14]), .Q3(SPY_PC[15]));
  _74LS163 _74ls163_5 (
    .nPE(and_12_out), .nSR(1'b1), .CP(or_14_out), .CET(_74ls163_4_tc), .CEP(1'b1), .P0(_74ls157_5_y1),
    .P1(_74ls157_5_y2), .P2(_74ls157_5_y3), .P3(_74ls157_5_y4), .TC(_74ls163_5_tc), .Q0(SPY_PC[16]),
    .Q1(SPY_PC[17]), .Q2(SPY_PC[18]), .Q3(SPY_PC[19]));
  _74LS163 _74ls163_6 (
    .nPE(and_12_out), .nSR(1'b1), .CP(or_14_out), .CET(_74ls163_5_tc), .CEP(1'b1), .P0(_74ls157_6_y1),
    .P1(_74ls157_6_y2), .P2(_74ls157_6_y3), .P3(_74ls157_6_y4), .TC(_74ls163_6_tc), .Q0(SPY_PC[20]),
    .Q1(SPY_PC[21]), .Q2(SPY_PC[22]), .Q3(PCneg));
  Half7474 half7474_13 (.nSD(1'b1), .D(1'b1), .CP(INTREQ), .nRD(and_15_out), .Q(half7474_13_q));  // open: nQ
  not not_15 (not_15_out, MopEnd);
  and and_13 (and_13_out, PCneg, not_16_out);
  not not_16 (not_16_out, PCbit0);
  // _74LS245 _74ls245_4: pin names not known; wires that end beside it: 1'b1, nE_PC
  // _74LS245 _74ls245_5: pin names not known; wires that end beside it: 1'b1, nE_PC
  // _74LS245 _74ls245_6: pin names not known; wires that end beside it: 1'b1, nE_PC
  Button I (.out(INTREQ));
  // Probe on and_13_out
  Half7474 half7474_14 (
    .nSD(1'b1), .D(half7474_13_q), .CP(not_15_out), .nRD(and_15_out), .Q(half7474_14_q), .nQ(half7474_14_nq));
  Half7474 half7474_15 (.nSD(1'b1), .D(1'b1), .CP(and_13_out), .nRD(and_14_out), .Q(half7474_15_q));  // open: nQ
  _74LS245 _74ls245_7 (
    .DIR(1'b1), .A1(1'b0), .A2(1'b1), .A3(1'b1), .A4(1'b0), .A5(1'b0), .A6(1'b0), .A7(1'b0), .A8(1'b0),
    .nOE(half7474_14_nq), .B1(DBUS[0]), .B2(DBUS[1]), .B3(DBUS[2]), .B4(DBUS[3]), .B5(DBUS[4]), .B6(DBUS[5]),
    .B7(DBUS[6]), .B8(DBUS[7]));
  _74LS245 _74ls245_8 (
    .DIR(1'b1), .A1(1'b0), .A2(1'b0), .A3(1'b0), .A4(1'b0), .A5(1'b0), .A6(1'b0), .A7(1'b0), .A8(1'b0),
    .nOE(half7474_14_nq), .B1(DBUS[8]), .B2(DBUS[9]), .B3(DBUS[10]), .B4(DBUS[11]), .B5(DBUS[12]),
    .B6(DBUS[13]), .B7(DBUS[14]), .B8(DBUS[15]));
  _74LS245 _74ls245_9 (
    .DIR(1'b1), .A1(1'b0), .A2(1'b0), .A3(1'b0), .A4(1'b0), .A5(1'b0), .A6(1'b0), .A7(1'b0), .A8(1'b0),
    .nOE(half7474_14_nq), .B1(DBUS[16]), .B2(DBUS[17]), .B3(DBUS[18]), .B4(DBUS[19]), .B5(DBUS[20]),
    .B6(DBUS[21]), .B7(DBUS[22]), .B8(DBUS[23]));
  Half7474 half7474_16 (
    .nSD(1'b1), .D(half7474_15_q), .CP(Tick), .nRD(and_14_out), .Q(half7474_16_q), .nQ(half7474_16_nq));
  and and_14 (and_14_out, nResetX, half7474_16_nq);
  LED led_12 (.in(TS0));
  Half7474 half7474_17 (.nSD(1'b1), .D(half7474_14_q), .CP(Tick), .nRD(and_15_out), .Q(half7474_17_q));  // open: nQ
  // Probe PC on {PCneg, SPY_PC, PCbit0}
  LED led_13 (.in(TS1));
  not not_17 (not_17_out, half7474_15_q);
  LED led_14 (.in(TS2));
  LED led_15 (.in(TS3));
  Half7474 half7474_18 (.nSD(1'b1), .D(half7474_17_q), .CP(Tick), .nRD(and_15_out), .Q(half7474_18_q));  // open: nQ
  LED led_16 (.in(TS4));
  Half7474 half7474_19 (.nSD(1'b1), .D(half7474_18_q), .CP(Tick), .nRD(and_15_out), .nQ(half7474_19_nq));  // open: Q
  LED led_17 (.in(TS5));
  or or_15 (or_15_out, half7474_18_q, half7474_16_q);
  LED led_18 (.in(TS6));
  _74LS574 _74ls574_8 (
    .nOC(not_17_out), .CLK(half7474_17_q), .D0(ABUS[0]), .D1(ABUS[1]), .D2(ABUS[2]), .D3(ABUS[3]),
    .D4(ABUS[4]), .D5(ABUS[5]), .D6(ABUS[6]), .D7(ABUS[7]), .Q0(DBUS[0]), .Q1(DBUS[1]), .Q2(DBUS[2]),
    .Q3(DBUS[3]), .Q4(DBUS[4]), .Q5(DBUS[5]), .Q6(DBUS[6]), .Q7(DBUS[7]));  // open: SPY
  _74LS574 _74ls574_9 (
    .nOC(not_17_out), .CLK(half7474_17_q), .D0(ABUS[8]), .D1(ABUS[9]), .D2(ABUS[10]), .D3(ABUS[11]),
    .D4(ABUS[12]), .D5(ABUS[13]), .D6(ABUS[14]), .D7(ABUS[15]), .Q0(DBUS[8]), .Q1(DBUS[9]), .Q2(DBUS[10]),
    .Q3(DBUS[11]), .Q4(DBUS[12]), .Q5(DBUS[13]), .Q6(DBUS[14]), .Q7(DBUS[15]));  // open: SPY
  _74LS574 _74ls574_10 (
    .nOC(not_17_out), .CLK(half7474_17_q), .D0(ABUS[16]), .D1(ABUS[17]), .D2(ABUS[18]), .D3(ABUS[19]),
    .D4(ABUS[20]), .D5(ABUS[21]), .D6(ABUS[22]), .D7(ABUS[23]), .Q0(DBUS[16]), .Q1(DBUS[17]), .Q2(DBUS[18]),
    .Q3(DBUS[19]), .Q4(DBUS[20]), .Q5(DBUS[21]), .Q6(DBUS[22]), .Q7(DBUS[23]));  // open: SPY
  and and_15 (and_15_out, nResetX, half7474_19_nq);
  // Probe on half7474_14_q
  or or_16 (or_16_out, half7474_14_q, half7474_15_q);
  // Probe on half7474_15_q
  Half7474 half7474_20 (.nSD(not_18_out), .D(1'b0), .CP(1'b1), .nRD(not_19_out), .Q(half7474_20_q));  // open: nQ
  not not_18 (not_18_out, half7474_14_q);
  not not_19 (not_19_out, half7474_15_q);
  // Probe on half7474_20_q
  // Probe on DBUS
  // Probe on PORT2OUT
  // Probe on or_16_out
  not not_20 (nBusRq, or_16_out);
  // _74LS245 _74ls245_10: pin names not known; wires that end beside it: 1'b1, half7474_14_nq, or_16_out, or_15_out, nBusRq, nE_PC, PC_LD, PC_CK

  // Other names for the same wires on the sheet: BAUD = clk_2; CK = XTAL; SPY_PC (some bits) = {PCneg, PCbit0}

  // Notes on the sheet:
  //   XTAL: Hz: 5
  //   GPIO2in: default 80
  //   clk: Hz: 4
  //   clk_2: Hz: 153600
  //   RUN/HALT
  //   CONTROL/SEQUENCER
  //   STEP
  //   RESET-F
  //   RESET-R
  //   microSTEP
  //   MEMORY
  //   MAR & NEG
  //   diode
  //   steering
  //   LATCHED SUBTRACTOR
  //   Out Enable
  //   Carry In
  //   U20
  //   U21
  //   MICROCODE
  //   GPIO
  //   GPIOw
  //   GPIOr
  //   if(a < 0) mem[b] += (int)getchar(); /* input */
  //           else if(b < 0) printf("%c", (char)mem[a]); /* output */
  //   stty -icanon -echo && nc localhost 23
  //   (-8)
  //   (-7)
  //   (-6)
  //   (-5)
  //   (-4) PORT2Write
  //   (-3)
  //   (-2)
  //   (-1) UARTtxdWrite
  //   (-4) PORT2read
  //   (-3) UARTbusyRead
  //   (-2) UARTavailRead
  //   (-1) UARTrxdRead
  //   UART
  //   ~D
  //   PROGRAM COUNTER
  //   ~Reset
  //   Flash
  //   ~OE
  //   ~LD
  //   CK
  //   NewPC
  //   INTERRUPT
  //   -----------------------
  //   Save current PC to holding register
  //   Set PC to 6
  //   RETURN FROM INTERRUPT
  //   (initiated by goto -2)
  //   -----------------------
  //   SET PC to holding register
  //   INTERUPT
  //   Neg
  //   Q
endmodule
