// Digital circuit Subtractor.dig as structural Verilog
module Subtractor (
  input  [23:0] B,
  input  nOE,
  input  nCY,
  input  [23:0] A,
  output [23:0] Q,
  output LEQ,
  output [23:0] Spy
);

  wire _74ls283_1_p2, _74ls283_2_p2, _74ls283_3_p2, _74ls283_4_p2, _74ls283_5_p2, nand_1_out, nand_2_out,
       nor_1_out, nor_2_out, nor_3_out, nor_4_out, nor_5_out, nor_6_out, nor_7_out, nor_8_out;
  wire [3:0] not_4_out, not_5_out, not_9_out, not_13_out, not_17_out, not_21_out;

  not not_1 (not_4_out[0], A[0]);
  not not_2 (not_4_out[1], A[1]);
  not not_3 (not_4_out[2], A[2]);
  not not_4 (not_4_out[3], A[3]);
  not not_5 (not_5_out[0], A[4]);
  not not_6 (not_5_out[1], A[5]);
  not not_7 (not_5_out[2], A[6]);
  not not_8 (not_5_out[3], A[7]);
  not not_9 (not_9_out[0], A[8]);
  not not_10 (not_9_out[1], A[9]);
  not not_11 (not_9_out[2], A[10]);
  not not_12 (not_9_out[3], A[11]);
  not not_13 (not_13_out[0], A[12]);
  not not_14 (not_13_out[1], A[13]);
  not not_15 (not_13_out[2], A[14]);
  not not_16 (not_13_out[3], A[15]);
  not not_17 (not_17_out[0], A[16]);
  not not_18 (not_17_out[1], A[17]);
  not not_19 (not_17_out[2], A[18]);
  not not_20 (not_17_out[3], A[19]);
  not not_21 (not_21_out[0], A[20]);
  not not_22 (not_21_out[1], A[21]);
  not not_23 (not_21_out[2], A[22]);
  not not_24 (not_21_out[3], A[23]);
  // _74LS283 _74ls283_1: pin names not known; wires that end beside it: nCY, _74ls283_1_p2
  // _74LS283 _74ls283_2: pin names not known; wires that end beside it: _74ls283_1_p2, _74ls283_2_p2
  nor nor_1 (nor_1_out, Spy[0], Spy[1], Spy[2]);
  nor nor_2 (nor_2_out, Spy[3], Spy[4], Spy[5]);
  nor nor_3 (nor_3_out, Spy[6], Spy[7], Spy[8]);
  nor nor_4 (nor_4_out, Spy[9], Spy[10], Spy[11]);
  nor nor_5 (nor_5_out, Spy[12], Spy[13], Spy[14]);
  nor nor_6 (nor_6_out, Spy[15], Spy[16], Spy[17]);
  nor nor_7 (nor_7_out, Spy[18], Spy[19], Spy[20]);
  nor nor_8 (nor_8_out, Spy[21], Spy[22], Spy[23]);
  // _74LS283 _74ls283_3: pin names not known; wires that end beside it: _74ls283_2_p2, _74ls283_3_p2
  nand nand_1 (nand_1_out, nor_1_out, nor_2_out, nor_3_out, nor_4_out, nor_5_out, nor_6_out, nor_7_out, nor_8_out);
  // _74LS283 _74ls283_4: pin names not known; wires that end beside it: _74ls283_3_p2, _74ls283_4_p2
  nand nand_2 (nand_2_out, Spy[23], Spy[23]);
  nand nand_3 (LEQ, nand_2_out, nand_1_out);
  // _74LS283 _74ls283_5: pin names not known; wires that end beside it: _74ls283_4_p2, _74ls283_5_p2
  // _74LS283 _74ls283_6: pin names not known; wires that end beside it: _74ls283_5_p2
  // _74LS245 _74ls245_1: pin names not known; wires that end beside it: 1'b1, nOE
  // _74LS245 _74ls245_2: pin names not known; wires that end beside it: 1'b1, nOE
  // _74LS245 _74ls245_3: pin names not known; wires that end beside it: 1'b1, nOE

  // Notes on the sheet:
  //   nOE: default 1
  //   nCY: default 1
endmodule
