// Digital circuit UART.dig as structural Verilog
module UART (
  input  [23:0] nD,
  input  BAUD,
  input  MopEnd,
  input  nReset,
  input  SendCk,
  input  Status,
  input  OE,
  output [23:0] nQ,
  output Busy,
  output driving
);

  wire _74ls165_1_qh, _74ls165_2_nqh, _74ls393_1__1qd, _74ls393_1__2qc, _74ls393_1__2qd, _74ls393_2__1qd,
       _74ls393_2__2qa, _74ls393_2__2qd, half7474_1_q, half7474_2_q, half7474_3_q, half7474_4_nq,
       half7474_5_q, nand_2_out, nand_3_out, nand_4_out, nand_5_out, nand_6_out, nand_7_out, nand_8_out,
       nand_9_out, not_1_out, not_2_out, not_3_out, not_4_out, not_5_out, not_6_out, not_7_out, reset_1_out,
       uart_telnet_gw_1_tx;
  wire [7:0] _74ls574_1_q0;

  Half7474 half7474_1 (.nSD(1'b1), .D(not_1_out), .CP(BAUD), .nRD(1'b1), .Q(half7474_1_q));  // open: nQ
  Half7474 half7474_2 (.nSD(half7474_1_q), .D(1'b0), .CP(SendCk), .nRD(1'b1), .Q(half7474_2_q));  // open: nQ
  _74LS574 _74ls574_1 (
    .nOC(1'b0), .CLK(SendCk), .D0(nD[0]), .D1(nD[1]), .D2(nD[2]), .D3(nD[3]), .D4(nD[4]), .D5(nD[5]),
    .D6(nD[6]), .D7(nD[7]), .Q0(_74ls574_1_q0[0]), .Q1(_74ls574_1_q0[1]), .Q2(_74ls574_1_q0[2]),
    .Q3(_74ls574_1_q0[3]), .Q4(_74ls574_1_q0[4]), .Q5(_74ls574_1_q0[5]), .Q6(_74ls574_1_q0[6]),
    .Q7(_74ls574_1_q0[7]));  // open: SPY
  nand nand_1 (Busy, half7474_2_q, nand_2_out);
  nand nand_2 (nand_2_out, Busy, nand_4_out);
  nand nand_3 (nand_3_out, nand_2_out, Status);
  _74LS393 _74ls393_1 (
    ._1A(BAUD), ._1CL(nand_2_out), ._2A(_74ls393_1__1qd), ._2CL(nand_2_out), ._1QD(_74ls393_1__1qd),
    ._2QC(_74ls393_1__2qc), ._2QD(_74ls393_1__2qd));  // open: _1QA, _1QB, _1QC, _2QA, _2QB
  not not_1 (not_1_out, _74ls393_1__1qd);
  nand nand_4 (nand_4_out, _74ls393_1__2qc, _74ls393_1__2qd);
  _74LS165 _74ls165_1 (
    .nLD(half7474_2_q), .INH(1'b0), .CLK(not_1_out), .SER(1'b0), .A(1'b0), .B(1'b0), .C(1'b0), .D(1'b0),
    .E(1'b0), .F(1'b0), .G(1'b0), .H(_74ls574_1_q0[7]), .QH(_74ls165_1_qh));  // open: nQH
  _74LS165 _74ls165_2 (
    .nLD(half7474_2_q), .INH(1'b0), .CLK(not_1_out), .SER(_74ls165_1_qh), .A(_74ls574_1_q0[6]),
    .B(_74ls574_1_q0[5]), .C(_74ls574_1_q0[4]), .D(_74ls574_1_q0[3]), .E(_74ls574_1_q0[2]),
    .F(_74ls574_1_q0[1]), .G(_74ls574_1_q0[0]), .H(1'b1), .nQH(_74ls165_2_nqh));  // open: QH
  Uart_Telnet_GW uart_telnet_gw_1 (.RX(_74ls165_2_nqh), .CLK(BAUD), .TX(uart_telnet_gw_1_tx));
  _74LS393 _74ls393_2 (
    ._1A(BAUD), ._1CL(not_3_out), ._2A(_74ls393_2__1qd), ._2CL(not_3_out), ._1QD(_74ls393_2__1qd),
    ._2QA(_74ls393_2__2qa), ._2QD(_74ls393_2__2qd));  // open: _1QA, _1QB, _1QC, _2QB, _2QC
  nand nand_5 (nand_5_out, half7474_5_q, OE);
  not not_2 (not_2_out, MopEnd);
  nand nand_6 (nand_6_out, _74ls393_2__2qa, _74ls393_2__2qd);
  not not_3 (not_3_out, not_5_out);
  Half7474 half7474_3 (.nSD(nand_5_out), .D(1'b0), .CP(nReset), .nRD(not_2_out), .Q(half7474_3_q));  // open: nQ
  not not_4 (not_4_out, nand_6_out);
  not not_5 (not_5_out, half7474_4_nq);
  nand nand_7 (nand_7_out, half7474_3_q, MopEnd);
  nand nand_8 (nand_8_out, _74ls393_2__1qd, not_4_out);
  not not_6 (not_6_out, uart_telnet_gw_1_tx);
  Half7474 half7474_4 (
    .nSD(uart_telnet_gw_1_tx), .D(1'b0), .CP(reset_1_out), .nRD(nand_8_out), .nQ(half7474_4_nq));  // open: Q
  Reset reset_1 (.out(reset_1_out));
  Half7474 half7474_5 (.nSD(nand_8_out), .D(1'b0), .CP(1'b0), .nRD(nand_7_out), .Q(half7474_5_q));  // open: nQ
  not not_7 (not_7_out, nand_5_out);
  // _74LS595 _74ls595_1: pin names not known; wires that end beside it: not_6_out, _74ls393_2__1qd, not_4_out, nand_5_out, 1'b1
  nand nand_9 (nand_9_out, not_7_out, OE);
  // Probe on nQ[7:0]
  assign nQ[15:8] = 1'b0 ? {8{1'b0}} : 8'bz;  // Driver driver_1
  assign nQ[23:16] = 1'b0 ? {8{1'b0}} : 8'bz;  // Driver driver_2
  and and_1 (driving, nand_9_out, nand_3_out);

  // Notes on the sheet:
  //   nD: default 16777045
  //   BAUD: Hz: 10
endmodule
