// Digital circuit UartRx.dig as structural Verilog
module UartRx (
  input  RX,
  input  nACK,
  input  nOE,
  input  CLK,
  output [7:0] nQ,
  output RDY
);

  wire _74ls393_1__1qd, _74ls393_1__2qa, _74ls393_1__2qd, half7474_1_nq, nand_1_out, nand_2_out, not_1_out,
       not_2_out, not_3_out, not_4_out, reset_1_out;

  _74LS393 _74ls393_1 (
    ._1A(CLK), ._1CL(not_1_out), ._2A(_74ls393_1__1qd), ._2CL(not_1_out), ._1QD(_74ls393_1__1qd),
    ._2QA(_74ls393_1__2qa), ._2QD(_74ls393_1__2qd));  // open: _1QA, _1QB, _1QC, _2QB, _2QC
  not not_1 (not_1_out, not_2_out);
  nand nand_1 (nand_1_out, _74ls393_1__2qa, _74ls393_1__2qd);
  not not_2 (not_2_out, half7474_1_nq);
  not not_3 (not_3_out, nand_1_out);
  // Probe on half7474_1_nq
  // Probe on _74ls393_1__1qd
  // Probe on not_3_out
  nand nand_2 (nand_2_out, _74ls393_1__1qd, not_3_out);
  Half7474 half7474_1 (.nSD(RX), .D(1'b0), .CP(reset_1_out), .nRD(nand_2_out), .nQ(half7474_1_nq));  // open: Q
  Reset reset_1 (.out(reset_1_out));
  // Probe on nand_2_out
  Half7474 half7474_2 (.nSD(nand_2_out), .D(1'b0), .CP(1'b0), .nRD(nACK), .Q(RDY));  // open: nQ
  not not_4 (not_4_out, RX);
  // _74595 _74595_1: pin names not known; wires that end beside it: not_4_out, _74ls393_1__1qd, not_3_out, nOE, 1'b1, 1'b1, 1'b0

  // Notes on the sheet:
  //   RX: default 1
  //   CLK: Hz: 16
endmodule
