// Digital circuit UartTx.dig as structural Verilog
module UartTx (
  input  [7:0] nD,
  input  STB,
  input  CLK,
  output TX,
  output BSY
);

  wire _74ls165_1_qh, _74ls393_1__1qd, _74ls393_1__2qa, _74ls393_1__2qd, nand_1_out, nand_3_out, nand_4_out,
       not_1_out, not_2_out, not_3_out, not_4_out;

  not not_1 (not_1_out, STB);
  not not_2 (not_2_out, not_3_out);
  not not_3 (not_3_out, not_1_out);
  nand nand_1 (nand_1_out, not_2_out, STB);
  // Probe on nand_1_out
  nand nand_2 (BSY, nand_1_out, nand_3_out);
  nand nand_3 (nand_3_out, BSY, nand_4_out);
  // Probe on BSY
  // Probe on nand_3_out
  _74LS393 _74ls393_1 (
    ._1A(CLK), ._1CL(nand_3_out), ._2A(_74ls393_1__1qd), ._2CL(nand_3_out), ._1QD(_74ls393_1__1qd),
    ._2QA(_74ls393_1__2qa), ._2QD(_74ls393_1__2qd));  // open: _1QA, _1QB, _1QC, _2QB, _2QC
  not not_4 (not_4_out, _74ls393_1__1qd);
  nand nand_4 (nand_4_out, _74ls393_1__2qa, _74ls393_1__2qd);
  // Probe on not_4_out
  _74LS165 _74ls165_1 (
    .nLD(nand_1_out), .INH(1'b0), .CLK(not_4_out), .SER(1'b0), .A(1'b0), .B(1'b0), .C(1'b0), .D(1'b0),
    .E(1'b0), .F(1'b0), .G(1'b0), .H(nD[7]), .QH(_74ls165_1_qh));  // open: nQH
  _74LS165 _74ls165_2 (
    .nLD(nand_1_out), .INH(1'b0), .CLK(not_4_out), .SER(_74ls165_1_qh), .A(nD[6]), .B(nD[5]), .C(nD[4]),
    .D(nD[3]), .E(nD[2]), .F(nD[1]), .G(nD[0]), .H(1'b1), .nQH(TX));  // open: QH

  // Notes on the sheet:
  //   nD: default 104
  //   CLK: Hz: 160
endmodule
