// Digital circuit Uart_Telnet_GW.dig as structural Verilog
module Uart_Telnet_GW (
  input  RX,
  input  CLK,
  output TX,
  output BSY
);

  wire _74ls165_1_qh, _74ls393_1__1qd, _74ls393_1__2qa, _74ls393_1__2qd, _74ls393_2__1qd, _74ls393_2__2qa,
       _74ls393_2__2qd, _74595_1_p9, and_1_out, d_ff_1_q, d_ff_2_q, d_ff_3_q, d_ff_4_q, d_ff_5_q, d_ff_6_q,
       d_ff_7_nq, delay_1_out, delay_2_out, delay_3_out, half7474_1_nq, half7474_2_q, nand_1_out, nand_2_out,
       nand_3_out, nand_5_out, nand_6_out, not_1_out, not_2_out, not_3_out, not_4_out, not_5_out, not_7_out,
       not_8_out, not_9_out, not_10_out, or_1_out, pulldown_1_out, pulldown_2_out, pulldown_3_out,
       pulldown_4_out, pulldown_10_out, pulldown_11_out, reset_1_out, telnet_1_av;
  wire [7:0] not_6_out, pulldown_9_out, telnet_1_out, undriven;

  _74LS393 _74ls393_1 (
    ._1A(CLK), ._1CL(not_1_out), ._2A(_74ls393_1__1qd), ._2CL(not_1_out), ._1QD(_74ls393_1__1qd),
    ._2QA(_74ls393_1__2qa), ._2QD(_74ls393_1__2qd));  // open: _1QA, _1QB, _1QC, _2QB, _2QC
  not not_1 (not_1_out, not_2_out);
  nand nand_1 (nand_1_out, _74ls393_1__2qa, _74ls393_1__2qd);
  not not_2 (not_2_out, half7474_1_nq);
  not not_3 (not_3_out, nand_1_out);
  // Probe on half7474_1_nq
  // Probe on _74ls393_1__1qd
  // Probe on not_3_out
  nand nand_2 (nand_2_out, _74ls393_1__1qd, not_3_out);
  Reset reset_1 (.out(reset_1_out));
  // Probe on nand_2_out
  not not_4 (not_4_out, RX);
  Half7474 half7474_1 (.nSD(RX), .D(1'b0), .CP(reset_1_out), .nRD(nand_2_out), .nQ(half7474_1_nq));  // open: Q
  Half7474 half7474_2 (.nSD(nand_2_out), .D(1'b0), .CP(1'b0), .nRD(not_5_out), .Q(half7474_2_q));  // open: nQ
  // _74595 _74595_1: pin names not known; wires that end beside it: not_4_out, _74ls393_1__1qd, not_3_out, 1'b0, 1'b1, 1'b1, 1'b0, CLK, _74595_1_p9
  UartRx uartrx_1 (
    .RX(pulldown_1_out), .nACK(pulldown_2_out), .nOE(pulldown_3_out), .CLK(pulldown_4_out));  // open: nQ, RDY
  PullDown pulldown_1 (.out(pulldown_1_out));
  PullDown pulldown_2 (.out(pulldown_2_out));
  PullDown pulldown_3 (.out(pulldown_3_out));
  PullDown pulldown_4 (.out(pulldown_4_out));
  not not_5 (not_5_out, delay_1_out);
  D_FF d_ff_1 (.D(1'b1), .C(CLK), .Q(d_ff_1_q));  // open: nQ
  Delay #(.delayTime(20)) delay_1 (.in(half7474_2_q), .out(delay_1_out));
  D_FF d_ff_2 (.D(d_ff_1_q), .C(CLK), .Q(d_ff_2_q));  // open: nQ
  assign not_6_out = ~undriven;  // Not not_6, 8 bits wide
  D_FF d_ff_3 (.D(d_ff_2_q), .C(CLK), .Q(d_ff_3_q));  // open: nQ
  Delay #(.delayTime(10)) delay_2 (.in(or_1_out), .out(delay_2_out));
  or or_1 (or_1_out, delay_3_out, half7474_2_q);
  D_FF d_ff_4 (.D(d_ff_3_q), .C(CLK), .Q(d_ff_4_q));  // open: nQ
  PullDown pulldown_5 (.out(delay_2_out));
  PullDown pulldown_6 (.out(half7474_2_q));
  and and_1 (and_1_out, d_ff_6_q, d_ff_7_nq);
  D_FF d_ff_5 (.D(d_ff_4_q), .C(CLK), .Q(d_ff_5_q));  // open: nQ
  not not_7 (not_7_out, _74595_1_p9);
  Telnet #(.telnetEscape("false")) telnet_1 (
    .in(not_6_out), .C(delay_2_out), .wr(half7474_2_q), .rd(telnet_1_av), .out(telnet_1_out), .av(telnet_1_av));
  PullDown pulldown_7 (.out(telnet_1_av));
  Delay #(.delayTime(5)) delay_3 (.in(telnet_1_av), .out(delay_3_out));
  // Probe on delay_3_out
  D_FF d_ff_6 (.D(d_ff_5_q), .C(CLK), .Q(d_ff_6_q));  // open: nQ
  not not_8 (not_8_out, not_9_out);
  not not_9 (not_9_out, not_7_out);
  // Probe on telnet_1_out
  PullDown #(.Bits(8)) pulldown_8 (.out(telnet_1_out));
  or or_2 (_74595_1_p9, delay_3_out, and_1_out);
  nand nand_3 (nand_3_out, not_8_out, _74595_1_p9);
  D_FF d_ff_7 (.D(d_ff_6_q), .C(CLK), .nQ(d_ff_7_nq));  // open: Q
  // Probe on nand_3_out
  nand nand_4 (BSY, nand_3_out, nand_5_out);
  nand nand_5 (nand_5_out, BSY, nand_6_out);
  // Probe on BSY
  // Probe on TX
  UartTx uarttx_1 (.nD(pulldown_9_out), .STB(pulldown_10_out), .CLK(pulldown_11_out));  // open: TX, BSY
  PullDown #(.Bits(8)) pulldown_9 (.out(pulldown_9_out));
  PullDown pulldown_10 (.out(pulldown_10_out));
  PullDown pulldown_11 (.out(pulldown_11_out));
  // Probe on nand_5_out
  _74LS393 _74ls393_2 (
    ._1A(CLK), ._1CL(nand_5_out), ._2A(_74ls393_2__1qd), ._2CL(nand_5_out), ._1QD(_74ls393_2__1qd),
    ._2QA(_74ls393_2__2qa), ._2QD(_74ls393_2__2qd));  // open: _1QA, _1QB, _1QC, _2QB, _2QC
  not not_10 (not_10_out, _74ls393_2__1qd);
  nand nand_6 (nand_6_out, _74ls393_2__2qa, _74ls393_2__2qd);
  // Probe on not_10_out
  _74LS165 _74ls165_1 (
    .nLD(nand_3_out), .INH(1'b0), .CLK(not_10_out), .SER(1'b0), .A(1'b0), .B(1'b0), .C(1'b0), .D(1'b0),
    .E(1'b0), .F(1'b0), .G(1'b0), .H(telnet_1_out[7]), .QH(_74ls165_1_qh));  // open: nQH
  _74LS165 _74ls165_2 (
    .nLD(nand_3_out), .INH(1'b0), .CLK(not_10_out), .SER(_74ls165_1_qh), .A(telnet_1_out[6]),
    .B(telnet_1_out[5]), .C(telnet_1_out[4]), .D(telnet_1_out[3]), .E(telnet_1_out[2]), .F(telnet_1_out[1]),
    .G(telnet_1_out[0]), .H(1'b1), .nQH(TX));  // open: QH

  // Notes on the sheet:
  //   CLK: Hz: 10
  //   SERIAL -> TELNET GATEWAY
  //   ONLY FOR TESTING IN SIMULATION
endmodule
